// Logisim project cpu.circ as structural Verilog: 15 circuits, main circuit main
module main (
  input  reset
);

  wire caddi, clk, Ekey, Eterm, keyboard_1_avail, memory_latch_1_oe_latched, memory_latch_1_we_latched,
       not_1_out, not_2_out, not_3_out, or_1_out, WEmem, WEreg;
  wire [2:0] ALUop, rd_writeReg, rs_read2, rt_read1, shamt, write_address;
  wire [3:0] opCode;
  wire [5:0] immediate;
  wire [6:0] bit_extender_2_out, keyboard_1_data;
  wire [15:0] ALUout, bit_extender_1_out, currentPC, fulladd_1_res, immediate16, instruction, KeyOut, L,
       memory_latch_1_address_latched, memory_latch_1_data_in_latched, memoryData, multiplexer_4_out,
       next_pc, NextPC_BEQ, NextPC_BLT, pcincrement, pcplusone, RS, RT, write_data;

  Keyboard keyboard_1 (.clk(clk), .re(Ekey), .clr(reset), .avail(keyboard_1_avail), .data(keyboard_1_data));
  assign bit_extender_1_out = {{9{1'b0}}, keyboard_1_data};  // Bit_Extender bit_extender_1
  controller controller_1 (
    .opCode(opCode), .caddi(caddi), .threedig(ALUop[2]), .twodig(ALUop[1]), .onedig(ALUop[0]), .WEmem(WEmem),
    .WEreg(WEreg), .Escreen(Eterm), .Ekey(Ekey));
  interpreter interpreter_1 (
    .instruc(instruction), .shAMt(shamt), .RD(rd_writeReg), .RS(rt_read1), .Rt(rs_read2), .imm(immediate),
    .address_j(L), .opcode(opCode));
  Multiplexer #(.width(16), .enable("false")) multiplexer_1 (
    .in0(16'h80), .in1(bit_extender_1_out), .out(KeyOut), .sel(keyboard_1_avail));
  not not_1 (not_1_out, or_1_out);
  or or_1 (or_1_out, RS[0], RS[1], RS[2], RS[3], RS[4], RS[5], RS[6], RS[7], RS[8], RS[9], RS[10], RS[11], RS[12], RS[13], RS[14], RS[15]);
  fulladd fulladd_1 (.sub(1'b1), .A(RS), .B(RT), .res(fulladd_1_res));  // open: ovf
  Multiplexer #(.width(16), .enable("false")) multiplexer_2 (
    .in0(pcplusone), .in1(pcincrement), .out(NextPC_BEQ), .sel(not_1_out));
  Multiplexer #(.width(16), .enable("false")) multiplexer_3 (
    .in0(pcplusone), .in1(pcincrement), .out(NextPC_BLT), .sel(fulladd_1_res[15]));
  ALU alu_1 (.in2(immediate16), .ALUout(pcincrement), .in1(pcplusone));  // open: opCode, sAmt
  Bit_Extender #(.in_width(16), .out_width(7)) bit_extender_2 (.in(RS), .out(bit_extender_2_out));
  TTY #(.rows(13), .cols(80)) tty_1 (.data(bit_extender_2_out), .clk(clk), .we(Eterm), .clr(reset));
  not not_2 (not_2_out, clk);
  not not_3 (not_3_out, clk);
  oneRegister oneregister_1 (.dataIn(next_pc), .reset(reset), .writeEnable(1'b1), .clk(not_2_out), .dataOut(currentPC));
  memory_latch memory_latch_1 (
    .address(ALUout), .WE(WEmem), .clk(not_3_out), .data_in(RT),
    .address_latched(memory_latch_1_address_latched), .WE_latched(memory_latch_1_we_latched),
    .OE_latched(memory_latch_1_oe_latched), .data_in_latched(memory_latch_1_data_in_latched));
  RegisterFile registerfile_1 (
    .RS(RS), .WE(WEreg), .Read2(rt_read1), .dataWrite(write_data), .Read1(rs_read2),
    .regWriteEnable(write_address), .Reset(reset), .RT(RT), .clk(clk));
  ROM #(.addrWidth(16), .dataWidth(16)) rom_1 (.addr(currentPC), .data(instruction));
  RAM #(.addrWidth(16), .dataWidth(16), .trigger("high"), .databus("bibus")) ram_1 (
    .addr(memory_latch_1_address_latched), .we(memory_latch_1_we_latched), .oe(memory_latch_1_oe_latched),
    .din(memory_latch_1_data_in_latched), .dout(memoryData));
  Clock clock_1 (.out(clk));
  signExtender signextender_1 (.inp(immediate), .outp(immediate16));
  ALU alu_2 (.in2(16'h1), .ALUout(pcplusone), .in1(currentPC), .opCode(3'b000));  // open: sAmt
  Multiplexer #(.width(16), .enable("false")) multiplexer_4 (
    .in0(RT), .in1(immediate16), .out(multiplexer_4_out), .sel(caddi));
  ALU alu_3 (.in2(multiplexer_4_out), .ALUout(ALUout), .in1(RS), .opCode(ALUop), .sAmt(shamt));
  Multiplexer #(.select(4), .width(3), .enable("false")) multiplexer_5 (
    .in0(rd_writeReg), .in1(rd_writeReg), .in2(rt_read1), .in3(rd_writeReg), .in4(rd_writeReg),
    .in5(rd_writeReg), .in6(rd_writeReg), .in7(rt_read1), .in13(3'b111), .in14(rd_writeReg),
    .out(write_address), .sel(opCode));  // open: in8, in9, in10, in11, in12, in15
  Multiplexer #(.select(4), .width(16), .enable("false")) multiplexer_6 (
    .in0(ALUout), .in1(ALUout), .in2(ALUout), .in3(ALUout), .in4(ALUout), .in5(ALUout), .in6(ALUout),
    .in7(memoryData), .in13(pcplusone), .in14(KeyOut), .out(write_data), .sel(opCode));  // open: in8, in9, in10, in11, in12, in15
  Multiplexer #(.select(4), .width(16), .enable("false")) multiplexer_7 (
    .in0(pcplusone), .in1(pcplusone), .in2(pcplusone), .in3(pcplusone), .in4(pcplusone), .in5(pcplusone),
    .in6(pcplusone), .in7(pcplusone), .in8(pcplusone), .in9(NextPC_BEQ), .in10(NextPC_BLT), .in11(L),
    .in12(RS), .in13(L), .in14(pcplusone), .in15(pcplusone), .out(next_pc), .sel(opCode));

  // Other names for the same wires on the sheet: rst = reset

  // Notes on the sheet:
  //   contents of rom_1 (hex, n*v repeats v):
  //   204a e008 22a0 f400 e008 22a0 f400 e008 22a0 f400 903f
endmodule

module ALU (
  input  [15:0] in1,
  input  [15:0] in2,
  input  [2:0] opCode,
  input  [2:0] sAmt,
  output [15:0] ALUout
);

  wire [15:0] addres, lres, Negres, rres, subres, XORres;

  assign Negres = ~in1;  // NOT_Gate not_1, 16 bits wide
  fulladd fulladd_1 (.sub(1'b0), .A(in1), .B(in2), .res(addres));  // open: ovf
  fulladd fulladd_2 (.sub(1'b1), .A(in1), .B(in2), .res(subres));  // open: ovf
  assign XORres = in2 ^ in1;  // XOR_Gate xor_1, 16 bits wide
  newleftShifter newleftshifter_1 (.A(in1), .shAmt(sAmt), .\final (lres));
  threeBitShifterRight threebitshifterright_1 (.A(in1), .shAmt(sAmt), .\final (rres));
  Multiplexer #(.select(3), .width(16), .enable("false")) multiplexer_1 (
    .in0(addres), .in1(subres), .in2(XORres), .in3(Negres), .in4(lres), .in5(rres), .out(ALUout), .sel(opCode));  // open: in6, in7
endmodule

module oneRegister (
  input  [15:0] dataIn,
  input  reset,
  input  writeEnable,
  input  clk,
  output [15:0] dataOut
);

  wire clk_t;

  and and_1 (clk_t, writeEnable, clk);
  D_Flip_Flop d_ff_1 (.D(dataIn[0]), .clk(clk_t), .Q(dataOut[0]), .reset(reset));  // open: Qn, preset
  D_Flip_Flop d_ff_2 (.D(dataIn[1]), .clk(clk_t), .Q(dataOut[1]), .reset(reset));  // open: Qn, preset
  D_Flip_Flop d_ff_3 (.D(dataIn[2]), .clk(clk_t), .Q(dataOut[2]), .reset(reset));  // open: Qn, preset
  D_Flip_Flop d_ff_4 (.D(dataIn[3]), .clk(clk_t), .Q(dataOut[3]), .reset(reset));  // open: Qn, preset
  D_Flip_Flop d_ff_5 (.D(dataIn[4]), .clk(clk_t), .Q(dataOut[4]), .reset(reset));  // open: Qn, preset
  D_Flip_Flop d_ff_6 (.D(dataIn[5]), .clk(clk_t), .Q(dataOut[5]), .reset(reset));  // open: Qn, preset
  D_Flip_Flop d_ff_7 (.D(dataIn[6]), .clk(clk_t), .Q(dataOut[6]), .reset(reset));  // open: Qn, preset
  D_Flip_Flop d_ff_8 (.D(dataIn[7]), .clk(clk_t), .Q(dataOut[7]), .reset(reset));  // open: Qn, preset
  D_Flip_Flop d_ff_9 (.D(dataIn[8]), .clk(clk_t), .Q(dataOut[8]), .reset(reset));  // open: Qn, preset
  D_Flip_Flop d_ff_10 (.D(dataIn[9]), .clk(clk_t), .Q(dataOut[9]), .reset(reset));  // open: Qn, preset
  D_Flip_Flop d_ff_11 (.D(dataIn[10]), .clk(clk_t), .Q(dataOut[10]), .reset(reset));  // open: Qn, preset
  D_Flip_Flop d_ff_12 (.D(dataIn[11]), .clk(clk_t), .Q(dataOut[11]), .reset(reset));  // open: Qn, preset
  D_Flip_Flop d_ff_13 (.D(dataIn[12]), .clk(clk_t), .Q(dataOut[12]), .reset(reset));  // open: Qn, preset
  D_Flip_Flop d_ff_14 (.D(dataIn[13]), .clk(clk_t), .Q(dataOut[13]), .reset(reset));  // open: Qn, preset
  D_Flip_Flop d_ff_15 (.D(dataIn[14]), .clk(clk_t), .Q(dataOut[14]), .reset(reset));  // open: Qn, preset
  D_Flip_Flop d_ff_16 (.D(dataIn[15]), .clk(clk_t), .Q(dataOut[15]), .reset(reset));  // open: Qn, preset

  // Other names for the same wires on the sheet: in0 = dataIn[0]; in1 = dataIn[1]; in2 = dataIn[2]; in3 = dataIn[3];
  //   in4 = dataIn[4]; in5 = dataIn[5]; in6 = dataIn[6]; in7 = dataIn[7]; in8 = dataIn[8]; in9 = dataIn[9];
  //   in10 = dataIn[10]; in11 = dataIn[11]; in12 = dataIn[12]; in13 = dataIn[13]; in14 = dataIn[14];
  //   in15 = dataIn[15]; o0 = dataOut[0]; o1 = dataOut[1]; o2 = dataOut[2]; o3 = dataOut[3]; o4 = dataOut[4];
  //   o5 = dataOut[5]; o6 = dataOut[6]; o7 = dataOut[7]; o8 = dataOut[8]; o9 = dataOut[9]; o10 = dataOut[10];
  //   o11 = dataOut[11]; o12 = dataOut[12]; o13 = dataOut[13]; o14 = dataOut[14]; o15 = dataOut[15]
endmodule

module RegisterFile (
  input  [15:0] dataWrite,
  input  [2:0] Read1,
  input  [2:0] Read2,
  input  [2:0] regWriteEnable,
  input  WE,
  input  clk,
  input  Reset,
  output [15:0] RS,
  output [15:0] RT
);

  wire a10, a11, a12, a13, a14, a15, a16, a17, b20, b21, b22, b23, b24, b25, b26, b27, WE0, WE1, WE2, WE3,
       WE4, WE5, WE6, WE7;
  wire [15:0] oneregister_1_dataout, oneregister_2_dataout, oneregister_3_dataout, oneregister_4_dataout,
       oneregister_5_dataout, oneregister_6_dataout, oneregister_7_dataout;

  Decoder #(.select(3)) decoder_1 (
    .out0(WE0), .out1(WE1), .out2(WE2), .out3(WE3), .out4(WE4), .out5(WE5), .out6(WE6), .out7(WE7),
    .sel(regWriteEnable), .en(WE));
  // Probe on {16{1'b0}}
  oneRegister oneregister_1 (
    .dataIn(dataWrite), .reset(Reset), .writeEnable(WE1), .clk(clk), .dataOut(oneregister_1_dataout));
  oneRegister oneregister_2 (
    .dataIn(dataWrite), .reset(Reset), .writeEnable(WE2), .clk(clk), .dataOut(oneregister_2_dataout));
  oneRegister oneregister_3 (
    .dataIn(dataWrite), .reset(Reset), .writeEnable(WE3), .clk(clk), .dataOut(oneregister_3_dataout));
  // Probe on oneregister_4_dataout
  oneRegister oneregister_4 (
    .dataIn(dataWrite), .reset(Reset), .writeEnable(WE4), .clk(clk), .dataOut(oneregister_4_dataout));
  // Probe on oneregister_5_dataout
  oneRegister oneregister_5 (
    .dataIn(dataWrite), .reset(Reset), .writeEnable(WE5), .clk(clk), .dataOut(oneregister_5_dataout));
  // Probe on oneregister_6_dataout
  oneRegister oneregister_6 (
    .dataIn(dataWrite), .reset(Reset), .writeEnable(WE6), .clk(clk), .dataOut(oneregister_6_dataout));
  oneRegister oneregister_7 (
    .dataIn(dataWrite), .reset(Reset), .writeEnable(WE7), .clk(clk), .dataOut(oneregister_7_dataout));
  // Probe on oneregister_1_dataout
  // Probe on oneregister_2_dataout
  // Probe on oneregister_3_dataout
  // Probe on oneregister_7_dataout
  Decoder #(.select(3)) decoder_2 (
    .out0(a10), .out1(a11), .out2(a12), .out3(a13), .out4(a14), .out5(a15), .out6(a16), .out7(a17),
    .sel(Read1));  // open: en
  assign RS = a10 ? {16{1'b0}} : 16'bz;  // Controlled_Buffer controlled_buffer_1
  assign RS = a11 ? oneregister_1_dataout : 16'bz;  // Controlled_Buffer controlled_buffer_2
  assign RS = a12 ? oneregister_2_dataout : 16'bz;  // Controlled_Buffer controlled_buffer_3
  assign RS = a13 ? oneregister_3_dataout : 16'bz;  // Controlled_Buffer controlled_buffer_4
  assign RS = a14 ? oneregister_4_dataout : 16'bz;  // Controlled_Buffer controlled_buffer_5
  assign RS = a15 ? oneregister_5_dataout : 16'bz;  // Controlled_Buffer controlled_buffer_6
  assign RS = a16 ? oneregister_6_dataout : 16'bz;  // Controlled_Buffer controlled_buffer_7
  assign RS = a17 ? oneregister_7_dataout : 16'bz;  // Controlled_Buffer controlled_buffer_8
  Decoder #(.select(3)) decoder_3 (
    .out0(b20), .out1(b21), .out2(b22), .out3(b23), .out4(b24), .out5(b25), .out6(b26), .out7(b27),
    .sel(Read2));  // open: en
  assign RT = b20 ? {16{1'b0}} : 16'bz;  // Controlled_Buffer controlled_buffer_9
  assign RT = b21 ? oneregister_1_dataout : 16'bz;  // Controlled_Buffer controlled_buffer_10
  assign RT = b22 ? oneregister_2_dataout : 16'bz;  // Controlled_Buffer controlled_buffer_11
  assign RT = b23 ? oneregister_3_dataout : 16'bz;  // Controlled_Buffer controlled_buffer_12
  assign RT = b24 ? oneregister_4_dataout : 16'bz;  // Controlled_Buffer controlled_buffer_13
  assign RT = b25 ? oneregister_5_dataout : 16'bz;  // Controlled_Buffer controlled_buffer_14
  assign RT = b26 ? oneregister_6_dataout : 16'bz;  // Controlled_Buffer controlled_buffer_15
  assign RT = b27 ? oneregister_7_dataout : 16'bz;  // Controlled_Buffer controlled_buffer_16

  // Other names for the same wires on the sheet: R1[15:0] = RS; R2[15:0] = RT; rst = Reset
endmodule

module controller (
  input  [3:0] opCode,
  output caddi,
  output threedig,
  output twodig,
  output onedig,
  output WEmem,
  output WEreg,
  output Escreen,
  output Ekey
);

  wire decoder_1_out0, decoder_1_out1, decoder_1_out2, decoder_1_out3, decoder_1_out4, decoder_1_out5,
       decoder_1_out6, decoder_1_out7, decoder_1_out13;

  Decoder #(.select(4)) decoder_1 (
    .out0(decoder_1_out0), .out1(decoder_1_out1), .out2(decoder_1_out2), .out3(decoder_1_out3),
    .out4(decoder_1_out4), .out5(decoder_1_out5), .out6(decoder_1_out6), .out7(decoder_1_out7), .out8(WEmem),
    .out13(decoder_1_out13), .out14(Ekey), .out15(Escreen), .sel(opCode));  // open: out9, out10, out11, out12, en
  or or_1 (WEreg, Ekey, decoder_1_out13, decoder_1_out7, decoder_1_out6, decoder_1_out5, decoder_1_out4, decoder_1_out3, decoder_1_out2, decoder_1_out1, decoder_1_out0);
  or or_2 (caddi, WEmem, decoder_1_out2, decoder_1_out7);
  or or_3 (threedig, decoder_1_out6, decoder_1_out5);
  or or_4 (twodig, decoder_1_out3, decoder_1_out4);
  or or_5 (onedig, decoder_1_out1, decoder_1_out6, decoder_1_out3);
endmodule

module interpreter (
  input  [15:0] instruc,
  output [2:0] shAMt,
  output [2:0] RD,
  output [2:0] RS,
  output [2:0] Rt,
  output [5:0] imm,
  output [15:0] address_j,
  output [3:0] opcode
);


  assign address_j = {4'b0000, instruc[11:0]};
  assign imm = instruc[5:0];
  assign opcode = instruc[15:12];
  assign RD = instruc[5:3];
  assign RS = instruc[8:6];
  assign Rt = instruc[11:9];
  assign shAMt = instruc[2:0];

  // Other names for the same wires on the sheet: addj[11:0] = instruc[11:0]; sh[2:0] = instruc[2:0];
  //   op[3:0] = instruc[15:12]
endmodule

module memory_latch (
  input  [15:0] address,
  input  WE,
  input  clk,
  input  [15:0] data_in,
  output [15:0] address_latched,
  output WE_latched,
  output OE_latched,
  output [15:0] data_in_latched
);

  wire DMwe_latch_q;
  wire [15:0] addr_latch_q;

  Register #(.width(16), .trigger("falling")) addr_latch (
    .D(address), .en(WE), .clk(clk), .Q(addr_latch_q));  // open: clr
  D_Flip_Flop #(.trigger("falling")) DMwe_latch (.D(WE), .clk(clk), .Q(DMwe_latch_q));  // open: Qn, preset, reset
  Register #(.width(16), .trigger("falling")) data_to_be_written (
    .D(data_in), .en(WE), .clk(clk), .Q(data_in_latched));  // open: clr
  Multiplexer #(.width(16), .enable("false")) multiplexer_1 (
    .in0(address), .in1(addr_latch_q), .out(address_latched), .sel(DMwe_latch_q));
  and and_1 (WE_latched, clk, DMwe_latch_q);
  not not_1 (OE_latched, WE_latched);
endmodule

module fulladd (
  input  sub,
  input  [15:0] A,
  input  [15:0] B,
  output ovf,
  output [15:0] res
);

  wire oneadd_1_ovf, oneadd_2_ovf, oneadd_3_ovf, oneadd_4_ovf, oneadd_5_ovf, oneadd_6_ovf, oneadd_7_ovf,
       oneadd_8_ovf, oneadd_9_ovf, oneadd_10_ovf, oneadd_11_ovf, oneadd_12_ovf, oneadd_13_ovf, oneadd_14_ovf,
       oneadd_15_ovf, oneadd_16_ovf, xor_1_out, xor_2_out, xor_3_out, xor_4_out, xor_5_out, xor_6_out,
       xor_7_out, xor_8_out, xor_9_out, xor_10_out, xor_11_out, xor_12_out, xor_13_out, xor_14_out,
       xor_15_out, xor_16_out;

  xor xor_1 (xor_1_out, B[0], sub);
  xor xor_2 (xor_2_out, B[1], sub);
  xor xor_3 (xor_3_out, B[2], sub);
  xor xor_4 (xor_4_out, B[3], sub);
  xor xor_5 (xor_5_out, B[4], sub);
  xor xor_6 (xor_6_out, B[5], sub);
  xor xor_7 (xor_7_out, B[6], sub);
  xor xor_8 (xor_8_out, B[7], sub);
  xor xor_9 (xor_9_out, B[8], sub);
  xor xor_10 (xor_10_out, B[9], sub);
  xor xor_11 (xor_11_out, B[10], sub);
  xor xor_12 (xor_12_out, B[11], sub);
  xor xor_13 (xor_13_out, B[12], sub);
  xor xor_14 (xor_14_out, B[13], sub);
  xor xor_15 (xor_15_out, B[14], sub);
  xor xor_16 (xor_16_out, B[15], sub);
  oneAdd oneadd_1 (.A(A[0]), .B(xor_1_out), .carryin(sub), .result(res[0]), .ovf(oneadd_1_ovf));
  oneAdd oneadd_2 (.A(A[1]), .B(xor_2_out), .carryin(oneadd_1_ovf), .result(res[1]), .ovf(oneadd_2_ovf));
  oneAdd oneadd_3 (.A(A[2]), .B(xor_3_out), .carryin(oneadd_2_ovf), .result(res[2]), .ovf(oneadd_3_ovf));
  oneAdd oneadd_4 (.A(A[3]), .B(xor_4_out), .carryin(oneadd_3_ovf), .result(res[3]), .ovf(oneadd_4_ovf));
  oneAdd oneadd_5 (.A(A[4]), .B(xor_5_out), .carryin(oneadd_4_ovf), .result(res[4]), .ovf(oneadd_5_ovf));
  oneAdd oneadd_6 (.A(A[5]), .B(xor_6_out), .carryin(oneadd_5_ovf), .result(res[5]), .ovf(oneadd_6_ovf));
  oneAdd oneadd_7 (.A(A[6]), .B(xor_7_out), .carryin(oneadd_6_ovf), .result(res[6]), .ovf(oneadd_7_ovf));
  oneAdd oneadd_8 (.A(A[7]), .B(xor_8_out), .carryin(oneadd_7_ovf), .result(res[7]), .ovf(oneadd_8_ovf));
  oneAdd oneadd_9 (.A(A[8]), .B(xor_9_out), .carryin(oneadd_8_ovf), .result(res[8]), .ovf(oneadd_9_ovf));
  oneAdd oneadd_10 (.A(A[9]), .B(xor_10_out), .carryin(oneadd_9_ovf), .result(res[9]), .ovf(oneadd_10_ovf));
  oneAdd oneadd_11 (.A(A[10]), .B(xor_11_out), .carryin(oneadd_10_ovf), .result(res[10]), .ovf(oneadd_11_ovf));
  oneAdd oneadd_12 (.A(A[11]), .B(xor_12_out), .carryin(oneadd_11_ovf), .result(res[11]), .ovf(oneadd_12_ovf));
  oneAdd oneadd_13 (.A(A[12]), .B(xor_13_out), .carryin(oneadd_12_ovf), .result(res[12]), .ovf(oneadd_13_ovf));
  oneAdd oneadd_14 (.A(A[13]), .B(xor_14_out), .carryin(oneadd_13_ovf), .result(res[13]), .ovf(oneadd_14_ovf));
  oneAdd oneadd_15 (.A(A[14]), .B(xor_15_out), .carryin(oneadd_14_ovf), .result(res[14]), .ovf(oneadd_15_ovf));
  oneAdd oneadd_16 (.A(A[15]), .B(xor_16_out), .carryin(oneadd_15_ovf), .result(res[15]), .ovf(oneadd_16_ovf));
  xor xor_17 (ovf, oneadd_15_ovf, oneadd_16_ovf);

  // Other names for the same wires on the sheet: a1 = A[0]; a2 = A[1]; a3 = A[2]; a4 = A[3]; a5 = A[4]; a6 = A[5];
  //   a7 = A[6]; a8 = A[7]; a9 = A[8]; a10 = A[9]; a11 = A[10]; a12 = A[11]; a13 = A[12]; a14 = A[13]; a15 = A[14];
  //   a16 = A[15]; b1 = B[0]; b2 = B[1]; b3 = B[2]; b4 = B[3]; b5 = B[4]; b6 = B[5]; b7 = B[6]; b8 = B[7]; b9 = B[8];
  //   b10 = B[9]; b11 = B[10]; b12 = B[11]; b13 = B[12]; b14 = B[13]; b15 = B[14]; b16 = B[15]
endmodule

module oneAdd (
  input  A,
  input  B,
  input  carryin,
  output result,
  output ovf
);

  wire and_1_out, and_2_out, xor_1_out;

  and and_1 (and_1_out, B, A);
  xor xor_1 (xor_1_out, A, B);
  or or_1 (ovf, and_1_out, and_2_out);
  and and_2 (and_2_out, xor_1_out, carryin);
  xor xor_2 (result, carryin, xor_1_out);

  // Other names for the same wires on the sheet: cy = carryin
endmodule

module newleftShifter (
  input  [15:0] A,
  input  [2:0] shAmt,
  output [15:0] \final 
);

  wire multiplexer_1_out, multiplexer_2_out, multiplexer_3_out, multiplexer_4_out, multiplexer_5_out,
       multiplexer_6_out, multiplexer_7_out, multiplexer_8_out, multiplexer_9_out, multiplexer_10_out,
       multiplexer_11_out, multiplexer_12_out, multiplexer_13_out, multiplexer_14_out, multiplexer_15_out,
       multiplexer_16_out, multiplexer_17_out, multiplexer_18_out, multiplexer_19_out, multiplexer_20_out,
       multiplexer_21_out, multiplexer_22_out, multiplexer_23_out, multiplexer_24_out, multiplexer_25_out,
       multiplexer_26_out, multiplexer_27_out, multiplexer_28_out, multiplexer_29_out, multiplexer_30_out,
       multiplexer_31_out, multiplexer_32_out, not_1_out, not_2_out, not_3_out;

  Multiplexer #(.enable("false")) multiplexer_1 (.in0(1'b0), .in1(A[0]), .out(multiplexer_1_out), .sel(not_1_out));
  Multiplexer #(.enable("false")) multiplexer_2 (.in0(A[0]), .in1(A[1]), .out(multiplexer_2_out), .sel(not_1_out));
  Multiplexer #(.enable("false")) multiplexer_3 (.in0(A[1]), .in1(A[2]), .out(multiplexer_3_out), .sel(not_1_out));
  Multiplexer #(.enable("false")) multiplexer_4 (.in0(A[2]), .in1(A[3]), .out(multiplexer_4_out), .sel(not_1_out));
  Multiplexer #(.enable("false")) multiplexer_5 (.in0(A[3]), .in1(A[4]), .out(multiplexer_5_out), .sel(not_1_out));
  Multiplexer #(.enable("false")) multiplexer_6 (.in0(A[4]), .in1(A[5]), .out(multiplexer_6_out), .sel(not_1_out));
  Multiplexer #(.enable("false")) multiplexer_7 (.in0(A[5]), .in1(A[6]), .out(multiplexer_7_out), .sel(not_1_out));
  Multiplexer #(.enable("false")) multiplexer_8 (.in0(A[6]), .in1(A[7]), .out(multiplexer_8_out), .sel(not_1_out));
  Multiplexer #(.enable("false")) multiplexer_9 (.in0(A[7]), .in1(A[8]), .out(multiplexer_9_out), .sel(not_1_out));
  Multiplexer #(.enable("false")) multiplexer_10 (.in0(A[8]), .in1(A[9]), .out(multiplexer_10_out), .sel(not_1_out));
  Multiplexer #(.enable("false")) multiplexer_11 (.in0(A[9]), .in1(A[10]), .out(multiplexer_11_out), .sel(not_1_out));
  Multiplexer #(.enable("false")) multiplexer_12 (.in0(A[10]), .in1(A[11]), .out(multiplexer_12_out), .sel(not_1_out));
  Multiplexer #(.enable("false")) multiplexer_13 (.in0(A[11]), .in1(A[12]), .out(multiplexer_13_out), .sel(not_1_out));
  Multiplexer #(.enable("false")) multiplexer_14 (.in0(A[12]), .in1(A[13]), .out(multiplexer_14_out), .sel(not_1_out));
  Multiplexer #(.enable("false")) multiplexer_15 (.in0(A[13]), .in1(A[14]), .out(multiplexer_15_out), .sel(not_1_out));
  Multiplexer #(.enable("false")) multiplexer_16 (.in0(A[14]), .in1(A[15]), .out(multiplexer_16_out), .sel(not_1_out));
  not not_1 (not_1_out, shAmt[0]);
  not not_2 (not_2_out, shAmt[1]);
  Multiplexer #(.enable("false")) multiplexer_17 (
    .in0(1'b0), .in1(multiplexer_1_out), .out(multiplexer_17_out), .sel(not_2_out));
  Multiplexer #(.enable("false")) multiplexer_18 (
    .in0(1'b0), .in1(multiplexer_2_out), .out(multiplexer_18_out), .sel(not_2_out));
  Multiplexer #(.enable("false")) multiplexer_19 (
    .in0(multiplexer_1_out), .in1(multiplexer_3_out), .out(multiplexer_19_out), .sel(not_2_out));
  Multiplexer #(.enable("false")) multiplexer_20 (
    .in0(multiplexer_2_out), .in1(multiplexer_4_out), .out(multiplexer_20_out), .sel(not_2_out));
  Multiplexer #(.enable("false")) multiplexer_21 (
    .in0(multiplexer_3_out), .in1(multiplexer_5_out), .out(multiplexer_21_out), .sel(not_2_out));
  Multiplexer #(.enable("false")) multiplexer_22 (
    .in0(multiplexer_4_out), .in1(multiplexer_6_out), .out(multiplexer_22_out), .sel(not_2_out));
  Multiplexer #(.enable("false")) multiplexer_23 (
    .in0(multiplexer_5_out), .in1(multiplexer_7_out), .out(multiplexer_23_out), .sel(not_2_out));
  Multiplexer #(.enable("false")) multiplexer_24 (
    .in0(multiplexer_6_out), .in1(multiplexer_8_out), .out(multiplexer_24_out), .sel(not_2_out));
  Multiplexer #(.enable("false")) multiplexer_25 (
    .in0(multiplexer_7_out), .in1(multiplexer_9_out), .out(multiplexer_25_out), .sel(not_2_out));
  Multiplexer #(.enable("false")) multiplexer_26 (
    .in0(multiplexer_8_out), .in1(multiplexer_10_out), .out(multiplexer_26_out), .sel(not_2_out));
  Multiplexer #(.enable("false")) multiplexer_27 (
    .in0(multiplexer_9_out), .in1(multiplexer_11_out), .out(multiplexer_27_out), .sel(not_2_out));
  Multiplexer #(.enable("false")) multiplexer_28 (
    .in0(multiplexer_10_out), .in1(multiplexer_12_out), .out(multiplexer_28_out), .sel(not_2_out));
  Multiplexer #(.enable("false")) multiplexer_29 (
    .in0(multiplexer_11_out), .in1(multiplexer_13_out), .out(multiplexer_29_out), .sel(not_2_out));
  Multiplexer #(.enable("false")) multiplexer_30 (
    .in0(multiplexer_12_out), .in1(multiplexer_14_out), .out(multiplexer_30_out), .sel(not_2_out));
  Multiplexer #(.enable("false")) multiplexer_31 (
    .in0(multiplexer_13_out), .in1(multiplexer_15_out), .out(multiplexer_31_out), .sel(not_2_out));
  Multiplexer #(.enable("false")) multiplexer_32 (
    .in0(multiplexer_14_out), .in1(multiplexer_16_out), .out(multiplexer_32_out), .sel(not_2_out));
  Multiplexer #(.enable("false")) multiplexer_33 (
    .in0(1'b0), .in1(multiplexer_17_out), .out(\final [0]), .sel(not_3_out));
  Multiplexer #(.enable("false")) multiplexer_34 (
    .in0(1'b0), .in1(multiplexer_18_out), .out(\final [1]), .sel(not_3_out));
  Multiplexer #(.enable("false")) multiplexer_35 (
    .in0(1'b0), .in1(multiplexer_19_out), .out(\final [2]), .sel(not_3_out));
  Multiplexer #(.enable("false")) multiplexer_36 (
    .in0(1'b0), .in1(multiplexer_20_out), .out(\final [3]), .sel(not_3_out));
  Multiplexer #(.enable("false")) multiplexer_37 (
    .in0(multiplexer_17_out), .in1(multiplexer_21_out), .out(\final [4]), .sel(not_3_out));
  Multiplexer #(.enable("false")) multiplexer_38 (
    .in0(multiplexer_18_out), .in1(multiplexer_22_out), .out(\final [5]), .sel(not_3_out));
  Multiplexer #(.enable("false")) multiplexer_39 (
    .in0(multiplexer_19_out), .in1(multiplexer_23_out), .out(\final [6]), .sel(not_3_out));
  Multiplexer #(.enable("false")) multiplexer_40 (
    .in0(multiplexer_20_out), .in1(multiplexer_24_out), .out(\final [7]), .sel(not_3_out));
  Multiplexer #(.enable("false")) multiplexer_41 (
    .in0(multiplexer_21_out), .in1(multiplexer_25_out), .out(\final [8]), .sel(not_3_out));
  Multiplexer #(.enable("false")) multiplexer_42 (
    .in0(multiplexer_22_out), .in1(multiplexer_26_out), .out(\final [9]), .sel(not_3_out));
  Multiplexer #(.enable("false")) multiplexer_43 (
    .in0(multiplexer_23_out), .in1(multiplexer_27_out), .out(\final [10]), .sel(not_3_out));
  Multiplexer #(.enable("false")) multiplexer_44 (
    .in0(multiplexer_24_out), .in1(multiplexer_28_out), .out(\final [11]), .sel(not_3_out));
  Multiplexer #(.enable("false")) multiplexer_45 (
    .in0(multiplexer_25_out), .in1(multiplexer_29_out), .out(\final [12]), .sel(not_3_out));
  Multiplexer #(.enable("false")) multiplexer_46 (
    .in0(multiplexer_26_out), .in1(multiplexer_30_out), .out(\final [13]), .sel(not_3_out));
  Multiplexer #(.enable("false")) multiplexer_47 (
    .in0(multiplexer_27_out), .in1(multiplexer_31_out), .out(\final [14]), .sel(not_3_out));
  Multiplexer #(.enable("false")) multiplexer_48 (
    .in0(multiplexer_28_out), .in1(multiplexer_32_out), .out(\final [15]), .sel(not_3_out));
  not not_3 (not_3_out, shAmt[2]);
endmodule

module threeBitShifterLeft (
  input  [15:0] A,
  input  [2:0] shAmt,
  output [15:0] \final 
);

  wire [15:0] twobitshifterleft_1_final;

  twoBitShifterLeft twobitshifterleft_1 (.A(A), .shAmt(shAmt[1:0]), .\final (twobitshifterleft_1_final));
  Multiplexer #(.enable("false")) multiplexer_1 (
    .in0(twobitshifterleft_1_final[0]), .in1(1'b0), .out(\final [0]), .sel(shAmt[2]));
  Multiplexer #(.enable("false")) multiplexer_2 (
    .in0(twobitshifterleft_1_final[1]), .in1(1'b0), .out(\final [1]), .sel(shAmt[2]));
  Multiplexer #(.enable("false")) multiplexer_3 (
    .in0(twobitshifterleft_1_final[2]), .in1(1'b0), .out(\final [2]), .sel(shAmt[2]));
  Multiplexer #(.enable("false")) multiplexer_4 (
    .in0(twobitshifterleft_1_final[3]), .in1(1'b0), .out(\final [3]), .sel(shAmt[2]));
  Multiplexer #(.enable("false")) multiplexer_5 (
    .in0(twobitshifterleft_1_final[4]), .in1(twobitshifterleft_1_final[0]), .out(\final [4]), .sel(shAmt[2]));
  Multiplexer #(.enable("false")) multiplexer_6 (
    .in0(twobitshifterleft_1_final[5]), .in1(twobitshifterleft_1_final[1]), .out(\final [5]), .sel(shAmt[2]));
  Multiplexer #(.enable("false")) multiplexer_7 (
    .in0(twobitshifterleft_1_final[6]), .in1(twobitshifterleft_1_final[2]), .out(\final [6]), .sel(shAmt[2]));
  Multiplexer #(.enable("false")) multiplexer_8 (
    .in0(twobitshifterleft_1_final[7]), .in1(twobitshifterleft_1_final[3]), .out(\final [7]), .sel(shAmt[2]));
  Multiplexer #(.enable("false")) multiplexer_9 (
    .in0(twobitshifterleft_1_final[8]), .in1(twobitshifterleft_1_final[4]), .out(\final [8]), .sel(shAmt[2]));
  Multiplexer #(.enable("false")) multiplexer_10 (
    .in0(twobitshifterleft_1_final[9]), .in1(twobitshifterleft_1_final[5]), .out(\final [9]), .sel(shAmt[2]));
  Multiplexer #(.enable("false")) multiplexer_11 (
    .in0(twobitshifterleft_1_final[10]), .in1(twobitshifterleft_1_final[6]), .out(\final [10]), .sel(shAmt[2]));
  Multiplexer #(.enable("false")) multiplexer_12 (
    .in0(twobitshifterleft_1_final[11]), .in1(twobitshifterleft_1_final[7]), .out(\final [11]), .sel(shAmt[2]));
  Multiplexer #(.enable("false")) multiplexer_13 (
    .in0(twobitshifterleft_1_final[12]), .in1(twobitshifterleft_1_final[8]), .out(\final [12]), .sel(shAmt[2]));
  Multiplexer #(.enable("false")) multiplexer_14 (
    .in0(twobitshifterleft_1_final[13]), .in1(twobitshifterleft_1_final[9]), .out(\final [13]), .sel(shAmt[2]));
  Multiplexer #(.enable("false")) multiplexer_15 (
    .in0(twobitshifterleft_1_final[14]), .in1(twobitshifterleft_1_final[10]), .out(\final [14]),
    .sel(shAmt[2]));
  Multiplexer #(.enable("false")) multiplexer_16 (
    .in0(twobitshifterleft_1_final[15]), .in1(twobitshifterleft_1_final[11]), .out(\final [15]),
    .sel(shAmt[2]));

  // Other names for the same wires on the sheet: bit0 = shAmt[0]; bit1 = shAmt[1]; in[15:0] = A; out[15:0] = \final ;
  //   bit2 = shAmt[2]
endmodule

module twoBitShifterLeft (
  input  [15:0] A,
  input  [1:0] shAmt,
  output [15:0] \final 
);

  wire [15:0] bitshifterleft_1_final;

  bitShifterLeft bitshifterleft_1 (.A(A), .shAmt(shAmt[0]), .\final (bitshifterleft_1_final));
  Multiplexer #(.enable("false")) multiplexer_1 (
    .in0(bitshifterleft_1_final[0]), .in1(1'b0), .out(\final [0]), .sel(shAmt[1]));
  Multiplexer #(.enable("false")) multiplexer_2 (
    .in0(bitshifterleft_1_final[1]), .in1(1'b0), .out(\final [1]), .sel(shAmt[1]));
  Multiplexer #(.enable("false")) multiplexer_3 (
    .in0(bitshifterleft_1_final[2]), .in1(bitshifterleft_1_final[0]), .out(\final [2]), .sel(shAmt[1]));
  Multiplexer #(.enable("false")) multiplexer_4 (
    .in0(bitshifterleft_1_final[3]), .in1(bitshifterleft_1_final[1]), .out(\final [3]), .sel(shAmt[1]));
  Multiplexer #(.enable("false")) multiplexer_5 (
    .in0(bitshifterleft_1_final[4]), .in1(bitshifterleft_1_final[2]), .out(\final [4]), .sel(shAmt[1]));
  Multiplexer #(.enable("false")) multiplexer_6 (
    .in0(bitshifterleft_1_final[5]), .in1(bitshifterleft_1_final[3]), .out(\final [5]), .sel(shAmt[1]));
  Multiplexer #(.enable("false")) multiplexer_7 (
    .in0(bitshifterleft_1_final[6]), .in1(bitshifterleft_1_final[4]), .out(\final [6]), .sel(shAmt[1]));
  Multiplexer #(.enable("false")) multiplexer_8 (
    .in0(bitshifterleft_1_final[7]), .in1(bitshifterleft_1_final[5]), .out(\final [7]), .sel(shAmt[1]));
  Multiplexer #(.enable("false")) multiplexer_9 (
    .in0(bitshifterleft_1_final[8]), .in1(bitshifterleft_1_final[6]), .out(\final [8]), .sel(shAmt[1]));
  Multiplexer #(.enable("false")) multiplexer_10 (
    .in0(bitshifterleft_1_final[9]), .in1(bitshifterleft_1_final[7]), .out(\final [9]), .sel(shAmt[1]));
  Multiplexer #(.enable("false")) multiplexer_11 (
    .in0(bitshifterleft_1_final[10]), .in1(bitshifterleft_1_final[8]), .out(\final [10]), .sel(shAmt[1]));
  Multiplexer #(.enable("false")) multiplexer_12 (
    .in0(bitshifterleft_1_final[11]), .in1(bitshifterleft_1_final[9]), .out(\final [11]), .sel(shAmt[1]));
  Multiplexer #(.enable("false")) multiplexer_13 (
    .in0(bitshifterleft_1_final[12]), .in1(bitshifterleft_1_final[10]), .out(\final [12]), .sel(shAmt[1]));
  Multiplexer #(.enable("false")) multiplexer_14 (
    .in0(bitshifterleft_1_final[13]), .in1(bitshifterleft_1_final[11]), .out(\final [13]), .sel(shAmt[1]));
  Multiplexer #(.enable("false")) multiplexer_15 (
    .in0(bitshifterleft_1_final[14]), .in1(bitshifterleft_1_final[12]), .out(\final [14]), .sel(shAmt[1]));
  Multiplexer #(.enable("false")) multiplexer_16 (
    .in0(bitshifterleft_1_final[15]), .out(\final [15]), .sel(shAmt[1]));  // open: in1

  // Other names for the same wires on the sheet: in[15:0] = A; out[15:0] = \final ; bit0 = shAmt[0]; bit1 = shAmt[1]
endmodule

module bitShifterLeft (
  input  [15:0] A,
  input  shAmt,
  output [15:0] \final 
);

  Multiplexer #(.enable("false")) multiplexer_1 (.in0(A[0]), .in1(1'b0), .out(\final [0]), .sel(shAmt));
  Multiplexer #(.enable("false")) multiplexer_2 (.in0(A[1]), .in1(A[0]), .out(\final [1]), .sel(shAmt));
  Multiplexer #(.enable("false")) multiplexer_3 (.in0(A[2]), .in1(A[1]), .out(\final [2]), .sel(shAmt));
  Multiplexer #(.enable("false")) multiplexer_4 (.in0(A[3]), .in1(A[2]), .out(\final [3]), .sel(shAmt));
  Multiplexer #(.enable("false")) multiplexer_5 (.in0(A[4]), .in1(A[3]), .out(\final [4]), .sel(shAmt));
  Multiplexer #(.enable("false")) multiplexer_6 (.in0(A[5]), .in1(A[4]), .out(\final [5]), .sel(shAmt));
  Multiplexer #(.enable("false")) multiplexer_7 (.in0(A[6]), .in1(A[5]), .out(\final [6]), .sel(shAmt));
  Multiplexer #(.enable("false")) multiplexer_8 (.in0(A[7]), .in1(A[6]), .out(\final [7]), .sel(shAmt));
  Multiplexer #(.enable("false")) multiplexer_9 (.in0(A[8]), .in1(A[7]), .out(\final [8]), .sel(shAmt));
  Multiplexer #(.enable("false")) multiplexer_10 (.in0(A[9]), .in1(A[8]), .out(\final [9]), .sel(shAmt));
  Multiplexer #(.enable("false")) multiplexer_11 (.in0(A[10]), .in1(A[9]), .out(\final [10]), .sel(shAmt));
  Multiplexer #(.enable("false")) multiplexer_12 (.in0(A[11]), .in1(A[10]), .out(\final [11]), .sel(shAmt));
  Multiplexer #(.enable("false")) multiplexer_13 (.in0(A[12]), .in1(A[11]), .out(\final [12]), .sel(shAmt));
  Multiplexer #(.enable("false")) multiplexer_14 (.in0(A[13]), .in1(A[12]), .out(\final [13]), .sel(shAmt));
  Multiplexer #(.enable("false")) multiplexer_15 (.in0(A[14]), .in1(A[13]), .out(\final [14]), .sel(shAmt));
  Multiplexer #(.enable("false")) multiplexer_16 (.in0(A[15]), .in1(A[14]), .out(\final [15]), .sel(shAmt));

  // Other names for the same wires on the sheet: bit0 = shAmt; in[15:0] = A; out[15:0] = \final 
endmodule

module threeBitShifterRight (
  input  [15:0] A,
  input  [2:0] shAmt,
  output [15:0] \final 
);

  threeBitShifterLeft threebitshifterleft_1 (
    .A({A[0], A[1], A[2], A[3], A[4], A[5], A[6], A[7], A[8], A[9], A[10], A[11], A[12], A[13], A[14], A[15]}),
    .shAmt(shAmt),
    .\final ({\final [0], \final [1], \final [2], \final [3], \final [4], \final [5], \final [6], \final [7], \final [8], \final [9], \final [10], \final [11], \final [12], \final [13], \final [14], \final [15]}));
endmodule

module signExtender (
  input  [5:0] inp,
  output [15:0] outp
);

  Multiplexer #(.width(10), .enable("false")) multiplexer_1 (
    .in0({10{1'b0}}), .in1({10{1'b1}}), .out(outp[15:6]), .sel(inp[5]));

  assign outp[5:0] = inp;
endmodule
