// Logisim project apple - Copy - Copy.circ as structural Verilog: 11 circuits, main circuit main
module main (
  input  reset
);

  wire addi_control, BTL, clk, EQz, keyboard_1_avail, KEYEN, memory_latch_1_oe_latched,
       memory_latch_1_we_latched, memWriteEn, not_1_out, not_3_out, or_1_out, regWriteEn, TTYEN;
  wire [2:0] ALUop, rd_writeReg, rs_read2, rt_read1, shamt, undriven, undriven_2, undriven_3, undriven_4,
       undriven_5, undriven_6, undriven_7, undriven_8, write_address;
  wire [3:0] opCode;
  wire [5:0] immediate;
  wire [6:0] bit_extender_2_out, keyboard_1_data;
  wire [14:0] add_sub_1_result;
  wire [15:0] ALUout, B, bit_extender_1_out, currentPC, immediate16, instruction, KeyOut, L,
       memory_latch_1_address_latched, memory_latch_1_data_in_latched, memoryData, multiplexer_7_out,
       next_pc, NextPC_BEQ, NextPC_BLT, PCplus1, RS, RT, undriven_9, undriven_10, undriven_11, undriven_12,
       undriven_13, undriven_14, write_data;

  Clock clock_1 (.out(clk));
  not not_1 (not_1_out, clk);
  opCodeControl opcodecontrol_1 (
    .opCode(opCode), .addi_control(addi_control), .alu_digit3(ALUop[2]), .alu_digit2(ALUop[1]),
    .alu_digit1(ALUop[0]), .memWriteEn(memWriteEn), .regWriteEn(regWriteEn), .screenEn(TTYEN), .KEYEN(KEYEN));
  or or_1 (or_1_out, RS[0], RS[1], RS[2], RS[3], RS[4], RS[5], RS[6], RS[7], RS[8], RS[9], RS[10], RS[11], RS[12], RS[13], RS[14], RS[15]);
  add_sub add_sub_1 (.sub(1'b1), .A(RS), .B(RT), .result({BTL, add_sub_1_result}));  // open: ovf
  register1 register1_1 (.regIn(next_pc), .reset(reset), .WE(1'b1), .clk(not_1_out), .regOut(currentPC));
  Format format_1 (
    .instruction(instruction), .shamt(shamt), .rd_writeReg(rd_writeReg), .rt_read1(rt_read1),
    .rs_read2(rs_read2), .immediate(immediate), .jAddress(L), .opCode(opCode));
  not not_2 (EQz, or_1_out);
  ALU alu_1 (.opCode(undriven), .in2(immediate16), .in1(PCplus1), .ALUout(B));  // open: shiftAmount
  Keyboard keyboard_1 (.clk(clk), .re(KEYEN), .clr(reset), .avail(keyboard_1_avail), .data(keyboard_1_data));
  ROM #(.addrWidth(16), .dataWidth(16)) rom_1 (.addr(currentPC), .data(instruction));
  // Probe on 16'h80
  Multiplexer #(.width(16), .enable("false")) multiplexer_1 (
    .in0(16'h80), .in1(bit_extender_1_out), .out(KeyOut), .sel(keyboard_1_avail));
  assign bit_extender_1_out = {{9{1'b0}}, keyboard_1_data};  // Bit_Extender bit_extender_1
  Multiplexer #(.width(16), .enable("false")) multiplexer_2 (.in0(PCplus1), .in1(B), .out(NextPC_BEQ), .sel(EQz));
  Multiplexer #(.width(16), .enable("false")) multiplexer_3 (.in0(PCplus1), .in1(B), .out(NextPC_BLT), .sel(BTL));
  ALU alu_2 (.opCode(3'b000), .in2(16'h1), .in1(currentPC), .ALUout(PCplus1), .shiftAmount(undriven_2));
  Bit_Extender #(.in_width(16), .out_width(7)) bit_extender_2 (.in(RS), .out(bit_extender_2_out));
  TTY #(.rows(13), .cols(80)) tty_1 (.data(bit_extender_2_out), .clk(clk), .we(TTYEN), .clr(reset));
  Multiplexer #(.select(4), .width(3), .enable("false")) multiplexer_4 (
    .in0(rd_writeReg), .in1(rd_writeReg), .in2(rt_read1), .in3(rd_writeReg), .in4(rd_writeReg),
    .in5(rd_writeReg), .in6(rd_writeReg), .in7(rt_read1), .in8(undriven_3), .in9(undriven_4),
    .in10(undriven_5), .in11(undriven_6), .in12(undriven_7), .in13(3'b111), .in14(rd_writeReg),
    .in15(undriven_8), .out(write_address), .sel(opCode));
  Multiplexer #(.select(4), .width(16), .enable("false")) multiplexer_5 (
    .in0(ALUout), .in1(ALUout), .in2(ALUout), .in3(ALUout), .in4(ALUout), .in5(ALUout), .in6(ALUout),
    .in7(memoryData), .in8(undriven_9), .in9(undriven_10), .in10(undriven_11), .in11(undriven_12),
    .in12(undriven_13), .in13(PCplus1), .in14(KeyOut), .in15(undriven_14), .out(write_data), .sel(opCode));
  Multiplexer #(.select(4), .width(16), .enable("false")) multiplexer_6 (
    .in0(PCplus1), .in1(PCplus1), .in2(PCplus1), .in3(PCplus1), .in4(PCplus1), .in5(PCplus1), .in6(PCplus1),
    .in7(PCplus1), .in8(PCplus1), .in9(NextPC_BEQ), .in10(NextPC_BLT), .in11(L), .in12(RS), .in13(L),
    .in14(PCplus1), .in15(PCplus1), .out(next_pc), .sel(opCode));
  not not_3 (not_3_out, clk);
  RegisterFile registerfile_1 (
    .RT(RT), .RS(RS), .Reset(reset), .globalWE(regWriteEn), .WriteReg(write_address), .Read2(rt_read1),
    .Read1(rs_read2), .WriteData(write_data), .clk(clk));
  memory_latch memory_latch_1 (
    .address(ALUout), .WE(memWriteEn), .clk(not_3_out), .data_in(RT),
    .address_latched(memory_latch_1_address_latched), .WE_latched(memory_latch_1_we_latched),
    .OE_latched(memory_latch_1_oe_latched), .data_in_latched(memory_latch_1_data_in_latched));
  assign immediate16 = {{10{immediate[5]}}, immediate};  // Bit_Extender bit_extender_3
  RAM #(.addrWidth(16), .dataWidth(16), .trigger("high"), .databus("bibus")) ram_1 (
    .addr(memory_latch_1_address_latched), .we(memory_latch_1_we_latched), .oe(memory_latch_1_oe_latched),
    .din(memory_latch_1_data_in_latched), .dout(memoryData));
  Multiplexer #(.width(16), .enable("false")) multiplexer_7 (
    .in0(RT), .in1(immediate16), .out(multiplexer_7_out), .sel(addi_control));
  // Probe on ALUop
  ALU alu_3 (.opCode(ALUop), .in2(multiplexer_7_out), .in1(RS), .ALUout(ALUout), .shiftAmount(shamt));

  // Notes on the sheet:
  //   IF RS < RT
  //   Calculate B = PC + 1 + IMM
  //   BEQZERO
  //   contents of rom_1 (hex, n*v repeats v):
  //   204a e008 22a0 f400 e008 22a0 f400 e008 22a0 f400 903f
  //   RS
  //   RT
endmodule

module addR (
  input  addA,
  input  addB,
  input  carryIN,
  input  addSub,
  output addSum,
  output carryOUT
);

  wire and_1_out, and_2_out, and_3_out, and_4_out, and_5_out, and_6_out, not_1_out, not_2_out, not_3_out,
       not_4_out, or_2_out, xor_1_out;

  xor xor_1 (xor_1_out, addSub, addA);
  and and_1 (and_1_out, xor_1_out, addB);
  not not_1 (not_1_out, xor_1_out);
  not not_2 (not_2_out, addB);
  or or_1 (carryOUT, and_1_out, and_4_out);
  and and_2 (and_2_out, not_1_out, addB);
  and and_3 (and_3_out, xor_1_out, not_2_out);
  and and_4 (and_4_out, or_2_out, carryIN);
  or or_2 (or_2_out, and_2_out, and_3_out);
  not not_3 (not_3_out, or_2_out);
  not not_4 (not_4_out, carryIN);
  and and_5 (and_5_out, not_3_out, carryIN);
  and and_6 (and_6_out, not_4_out, or_2_out);
  or or_3 (addSum, and_5_out, and_6_out);
endmodule

module add_sub (
  input  sub,
  input  [15:0] A,
  input  [15:0] B,
  output ovf,
  output [15:0] result
);

  wire add1_carryout, add2_carryout, add3_carryout, add4_carryout, add5_carryout, add6_carryout,
       add7_carryout, add8_carryout, add9_carryout, add10_carryout, add11_carryout, add12_carryout,
       add13_carryout, add14_carryout, add15_carryout, add16_carryout;

  addR add1 (.addA(B[0]), .addB(A[0]), .carryIN(sub), .addSub(sub), .addSum(result[0]), .carryOUT(add1_carryout));
  addR add2 (
    .addA(B[1]), .addB(A[1]), .carryIN(add1_carryout), .addSub(sub), .addSum(result[1]),
    .carryOUT(add2_carryout));
  addR add3 (
    .addA(B[2]), .addB(A[2]), .carryIN(add2_carryout), .addSub(sub), .addSum(result[2]),
    .carryOUT(add3_carryout));
  addR add4 (
    .addA(B[3]), .addB(A[3]), .carryIN(add3_carryout), .addSub(sub), .addSum(result[3]),
    .carryOUT(add4_carryout));
  addR add5 (
    .addA(B[4]), .addB(A[4]), .carryIN(add4_carryout), .addSub(sub), .addSum(result[4]),
    .carryOUT(add5_carryout));
  addR add6 (
    .addA(B[5]), .addB(A[5]), .carryIN(add5_carryout), .addSub(sub), .addSum(result[5]),
    .carryOUT(add6_carryout));
  addR add7 (
    .addA(B[6]), .addB(A[6]), .carryIN(add6_carryout), .addSub(sub), .addSum(result[6]),
    .carryOUT(add7_carryout));
  addR add8 (
    .addA(B[7]), .addB(A[7]), .carryIN(add7_carryout), .addSub(sub), .addSum(result[7]),
    .carryOUT(add8_carryout));
  addR add9 (
    .addA(B[8]), .addB(A[8]), .carryIN(add8_carryout), .addSub(sub), .addSum(result[8]),
    .carryOUT(add9_carryout));
  addR add10 (
    .addA(B[9]), .addB(A[9]), .carryIN(add9_carryout), .addSub(sub), .addSum(result[9]),
    .carryOUT(add10_carryout));
  addR add11 (
    .addA(B[10]), .addB(A[10]), .carryIN(add10_carryout), .addSub(sub), .addSum(result[10]),
    .carryOUT(add11_carryout));
  addR add12 (
    .addA(B[11]), .addB(A[11]), .carryIN(add11_carryout), .addSub(sub), .addSum(result[11]),
    .carryOUT(add12_carryout));
  addR add13 (
    .addA(B[12]), .addB(A[12]), .carryIN(add12_carryout), .addSub(sub), .addSum(result[12]),
    .carryOUT(add13_carryout));
  addR add14 (
    .addA(B[13]), .addB(A[13]), .carryIN(add13_carryout), .addSub(sub), .addSum(result[13]),
    .carryOUT(add14_carryout));
  addR add15 (
    .addA(B[14]), .addB(A[14]), .carryIN(add14_carryout), .addSub(sub), .addSum(result[14]),
    .carryOUT(add15_carryout));
  xor xor_1 (ovf, add15_carryout, add16_carryout);
  addR add16 (
    .addA(B[15]), .addB(A[15]), .carryIN(add15_carryout), .addSub(sub), .addSum(result[15]),
    .carryOUT(add16_carryout));
endmodule

module ALU (
  input  [15:0] in1,
  input  [15:0] in2,
  input  [2:0] opCode,
  input  [2:0] shiftAmount,
  output [15:0] ALUout
);

  wire [15:0] add_sub_1_result, add_sub_2_result, leftshift_1_shifted, not_1_out, rightshift_1_out_3,
       xor_1_out;

  assign xor_1_out = in2 ^ in1;  // XOR_Gate xor_1, 16 bits wide
  assign not_1_out = ~in1;  // NOT_Gate not_1, 16 bits wide
  add_sub add_sub_1 (.sub(1'b0), .A(in1), .B(in2), .result(add_sub_1_result));  // open: ovf
  add_sub add_sub_2 (.sub(1'b1), .A(in1), .B(in2), .result(add_sub_2_result));  // open: ovf
  leftShift leftshift_1 (.data(in1), .shiftAmount(shiftAmount), .shifted(leftshift_1_shifted));
  rightShift rightshift_1 (.data(in1), .shiftAmount(shiftAmount), .out_3(rightshift_1_out_3));
  Multiplexer #(.select(3), .width(16), .enable("false")) multiplexer_1 (
    .in0(add_sub_1_result), .in1(add_sub_2_result), .in2(xor_1_out), .in3(not_1_out),
    .in4(leftshift_1_shifted), .in5(rightshift_1_out_3), .out(ALUout), .sel(opCode));  // open: in6, in7
endmodule

module register1 (
  input  [15:0] regIn,
  input  reset,
  input  WE,
  input  clk,
  output [15:0] regOut
);

  wire and_1_out, and_2_out, and_3_out, and_4_out, and_5_out, and_6_out, and_7_out, and_8_out, and_9_out,
       and_10_out, and_11_out, and_12_out, and_13_out, and_14_out, and_15_out, and_16_out;

  D_Flip_Flop d_ff_1 (.D(regIn[0]), .clk(and_1_out), .Q(regOut[0]), .reset(reset));  // open: Qn, preset
  and and_1 (and_1_out, WE, clk);
  and and_2 (and_2_out, WE, clk);
  D_Flip_Flop d_ff_2 (.D(regIn[2]), .clk(and_3_out), .Q(regOut[2]), .reset(reset));  // open: Qn, preset
  and and_3 (and_3_out, WE, clk);
  and and_4 (and_4_out, WE, clk);
  and and_5 (and_5_out, WE, clk);
  and and_6 (and_6_out, WE, clk);
  and and_7 (and_7_out, WE, clk);
  and and_8 (and_8_out, WE, clk);
  and and_9 (and_9_out, WE, clk);
  and and_10 (and_10_out, WE, clk);
  and and_11 (and_11_out, WE, clk);
  and and_12 (and_12_out, WE, clk);
  and and_13 (and_13_out, WE, clk);
  and and_14 (and_14_out, WE, clk);
  D_Flip_Flop d_ff_3 (.D(regIn[1]), .clk(and_2_out), .Q(regOut[1]), .reset(reset));  // open: Qn, preset
  D_Flip_Flop d_ff_4 (.D(regIn[3]), .clk(and_4_out), .Q(regOut[3]), .reset(reset));  // open: Qn, preset
  D_Flip_Flop d_ff_5 (.D(regIn[4]), .clk(and_5_out), .Q(regOut[4]), .reset(reset));  // open: Qn, preset
  D_Flip_Flop d_ff_6 (.D(regIn[5]), .clk(and_6_out), .Q(regOut[5]), .reset(reset));  // open: Qn, preset
  D_Flip_Flop d_ff_7 (.D(regIn[6]), .clk(and_7_out), .Q(regOut[6]), .reset(reset));  // open: Qn, preset
  D_Flip_Flop d_ff_8 (.D(regIn[7]), .clk(and_8_out), .Q(regOut[7]), .reset(reset));  // open: Qn, preset
  D_Flip_Flop d_ff_9 (.D(regIn[8]), .clk(and_9_out), .Q(regOut[8]), .reset(reset));  // open: Qn, preset
  D_Flip_Flop d_ff_10 (.D(regIn[9]), .clk(and_10_out), .Q(regOut[9]), .reset(reset));  // open: Qn, preset
  D_Flip_Flop d_ff_11 (.D(regIn[10]), .clk(and_11_out), .Q(regOut[10]), .reset(reset));  // open: Qn, preset
  D_Flip_Flop d_ff_12 (.D(regIn[11]), .clk(and_12_out), .Q(regOut[11]), .reset(reset));  // open: Qn, preset
  D_Flip_Flop d_ff_13 (.D(regIn[12]), .clk(and_13_out), .Q(regOut[12]), .reset(reset));  // open: Qn, preset
  D_Flip_Flop d_ff_14 (.D(regIn[13]), .clk(and_15_out), .Q(regOut[13]), .reset(reset));  // open: Qn, preset
  and and_15 (and_15_out, WE, clk);
  D_Flip_Flop d_ff_15 (.D(regIn[14]), .clk(and_14_out), .Q(regOut[14]), .reset(reset));  // open: Qn, preset
  D_Flip_Flop d_ff_16 (.D(regIn[15]), .clk(and_16_out), .Q(regOut[15]), .reset(reset));  // open: Qn, preset
  and and_16 (and_16_out, WE, clk);

  // Other names for the same wires on the sheet: in0 = regIn[0]; in1 = regIn[1]; in2 = regIn[2]; in3 = regIn[3];
  //   in4 = regIn[4]; in5 = regIn[5]; in6 = regIn[6]; in7 = regIn[7]; in8 = regIn[8]; in9 = regIn[9];
  //   in10 = regIn[10]; in11 = regIn[11]; in12 = regIn[12]; in13 = regIn[13]; in14 = regIn[14]; in15 = regIn[15];
  //   out0 = regOut[0]; out1 = regOut[1]; out2 = regOut[2]; out3 = regOut[3]; out4 = regOut[4]; out5 = regOut[5];
  //   out6 = regOut[6]; out7 = regOut[7]; out8 = regOut[8]; out9 = regOut[9]; out10 = regOut[10]; out11 = regOut[11];
  //   out12 = regOut[12]; out13 = regOut[13]; out14 = regOut[14]; out15 = regOut[15]
endmodule

module RegisterFile (
  input  [15:0] WriteData,
  input  [2:0] Read1,
  input  [2:0] Read2,
  input  [2:0] WriteReg,
  input  globalWE,
  input  clk,
  input  Reset,
  output [15:0] RS,
  output [15:0] RT
);

  wire RE10, RE11, RE12, RE13, RE14, RE15, RE16, RE17, RE20, RE21, RE22, RE23, RE24, RE25, RE26, RE27, WE0,
       WE1, WE2, WE3, WE4, WE5, WE6, WE7;
  wire [15:0] out1, out2, out3, out4, out5, out6, out7;

  Decoder #(.select(3)) decoder_1 (
    .out0(WE0), .out1(WE1), .out2(WE2), .out3(WE3), .out4(WE4), .out5(WE5), .out6(WE6), .out7(WE7),
    .sel(WriteReg), .en(globalWE));
  // Probe on out1
  // Probe on {16{1'b0}}
  register1 register1_1 (.regIn(WriteData), .reset(Reset), .WE(WE1), .clk(clk), .regOut(out1));
  // Probe on out2
  register1 register1_2 (.regIn(WriteData), .reset(Reset), .WE(WE2), .clk(clk), .regOut(out2));
  // Probe on out3
  register1 register1_3 (.regIn(WriteData), .reset(Reset), .WE(WE3), .clk(clk), .regOut(out3));
  // Probe on out4
  register1 register1_4 (.regIn(WriteData), .reset(Reset), .WE(WE4), .clk(clk), .regOut(out4));
  // Probe on out5
  register1 register1_5 (.regIn(WriteData), .reset(Reset), .WE(WE5), .clk(clk), .regOut(out5));
  // Probe on out6
  register1 register1_6 (.regIn(WriteData), .reset(Reset), .WE(WE6), .clk(clk), .regOut(out6));
  // Probe on out7
  register1 register1_7 (.regIn(WriteData), .reset(Reset), .WE(WE7), .clk(clk), .regOut(out7));
  Decoder #(.select(3)) decoder_2 (
    .out0(RE10), .out1(RE11), .out2(RE12), .out3(RE13), .out4(RE14), .out5(RE15), .out6(RE16), .out7(RE17),
    .sel(Read1));  // open: en
  assign RS = RE10 ? {16{1'b0}} : 16'bz;  // Controlled_Buffer controlled_buffer_1
  assign RS = RE11 ? out1 : 16'bz;  // Controlled_Buffer controlled_buffer_2
  assign RS = RE12 ? out2 : 16'bz;  // Controlled_Buffer controlled_buffer_3
  assign RS = RE13 ? out3 : 16'bz;  // Controlled_Buffer controlled_buffer_4
  assign RS = RE14 ? out4 : 16'bz;  // Controlled_Buffer controlled_buffer_5
  assign RS = RE15 ? out5 : 16'bz;  // Controlled_Buffer controlled_buffer_6
  assign RS = RE16 ? out6 : 16'bz;  // Controlled_Buffer controlled_buffer_7
  assign RS = RE17 ? out7 : 16'bz;  // Controlled_Buffer controlled_buffer_8
  Decoder #(.select(3)) decoder_3 (
    .out0(RE20), .out1(RE21), .out2(RE22), .out3(RE23), .out4(RE24), .out5(RE25), .out6(RE26), .out7(RE27),
    .sel(Read2));  // open: en
  assign RT = RE20 ? {16{1'b0}} : 16'bz;  // Controlled_Buffer controlled_buffer_9
  assign RT = RE21 ? out1 : 16'bz;  // Controlled_Buffer controlled_buffer_10
  assign RT = RE22 ? out2 : 16'bz;  // Controlled_Buffer controlled_buffer_11
  assign RT = RE23 ? out3 : 16'bz;  // Controlled_Buffer controlled_buffer_12
  assign RT = RE24 ? out4 : 16'bz;  // Controlled_Buffer controlled_buffer_13
  assign RT = RE25 ? out5 : 16'bz;  // Controlled_Buffer controlled_buffer_14
  assign RT = RE26 ? out6 : 16'bz;  // Controlled_Buffer controlled_buffer_15
  assign RT = RE27 ? out7 : 16'bz;  // Controlled_Buffer controlled_buffer_16

  // Other names for the same wires on the sheet: ReadOut1[15:0] = RS; ReadOut2[15:0] = RT
endmodule

module opCodeControl (
  input  [3:0] opCode,
  output addi_control,
  output alu_digit3,
  output alu_digit2,
  output alu_digit1,
  output memWriteEn,
  output regWriteEn,
  output screenEn,
  output KEYEN
);

  wire decoder_1_out0, decoder_1_out1, decoder_1_out2, decoder_1_out3, decoder_1_out4, decoder_1_out5,
       decoder_1_out6, decoder_1_out7, decoder_1_out13;

  Decoder #(.select(4)) decoder_1 (
    .out0(decoder_1_out0), .out1(decoder_1_out1), .out2(decoder_1_out2), .out3(decoder_1_out3),
    .out4(decoder_1_out4), .out5(decoder_1_out5), .out6(decoder_1_out6), .out7(decoder_1_out7),
    .out8(memWriteEn), .out13(decoder_1_out13), .out14(KEYEN), .out15(screenEn), .sel(opCode));  // open: out9, out10, out11, out12, en
  or regWrEn (regWriteEn, KEYEN, decoder_1_out13, decoder_1_out7, decoder_1_out6, decoder_1_out5, decoder_1_out4, decoder_1_out3, decoder_1_out2, decoder_1_out1, decoder_1_out0);
  or or_1 (addi_control, memWriteEn, decoder_1_out2, decoder_1_out7);
  or or_2 (alu_digit3, decoder_1_out6, decoder_1_out5);
  or or_3 (alu_digit2, decoder_1_out3, decoder_1_out4);
  or or_4 (alu_digit1, decoder_1_out1, decoder_1_out6, decoder_1_out3);
endmodule

module Format (
  input  [15:0] instruction,
  output [2:0] shamt,
  output [2:0] rd_writeReg,
  output [2:0] rt_read1,
  output [2:0] rs_read2,
  output [5:0] immediate,
  output [15:0] jAddress,
  output [3:0] opCode
);


  assign immediate = instruction[5:0];
  assign jAddress = {4'b0000, instruction[11:0]};
  assign opCode = instruction[15:12];
  assign rd_writeReg = instruction[5:3];
  assign rs_read2 = instruction[11:9];
  assign rt_read1 = instruction[8:6];
  assign shamt = instruction[2:0];
endmodule

module leftShift (
  input  [15:0] data,
  input  [2:0] shiftAmount,
  output [15:0] shifted
);

  wire multiplexer_1_out, multiplexer_2_out, multiplexer_3_out, multiplexer_4_out, multiplexer_5_out,
       multiplexer_6_out, multiplexer_7_out, multiplexer_8_out, multiplexer_9_out, multiplexer_10_out,
       multiplexer_11_out, multiplexer_12_out, multiplexer_13_out, multiplexer_14_out, multiplexer_15_out,
       multiplexer_16_out, multiplexer_17_out, multiplexer_18_out, multiplexer_19_out, multiplexer_20_out,
       multiplexer_21_out, multiplexer_22_out, multiplexer_23_out, multiplexer_24_out, multiplexer_25_out,
       multiplexer_26_out, multiplexer_27_out, multiplexer_28_out, multiplexer_29_out, multiplexer_30_out,
       multiplexer_31_out, multiplexer_32_out, not_1_out, not_2_out, not_3_out;

  Multiplexer #(.enable("false")) multiplexer_1 (.in0(1'b0), .in1(data[0]), .out(multiplexer_1_out), .sel(not_1_out));
  Multiplexer #(.enable("false")) multiplexer_2 (
    .in0(data[0]), .in1(data[1]), .out(multiplexer_2_out), .sel(not_1_out));
  Multiplexer #(.enable("false")) multiplexer_3 (
    .in0(data[1]), .in1(data[2]), .out(multiplexer_3_out), .sel(not_1_out));
  Multiplexer #(.enable("false")) multiplexer_4 (
    .in0(data[2]), .in1(data[3]), .out(multiplexer_4_out), .sel(not_1_out));
  Multiplexer #(.enable("false")) multiplexer_5 (
    .in0(data[3]), .in1(data[4]), .out(multiplexer_5_out), .sel(not_1_out));
  Multiplexer #(.enable("false")) multiplexer_6 (
    .in0(data[4]), .in1(data[5]), .out(multiplexer_6_out), .sel(not_1_out));
  Multiplexer #(.enable("false")) multiplexer_7 (
    .in0(data[5]), .in1(data[6]), .out(multiplexer_7_out), .sel(not_1_out));
  Multiplexer #(.enable("false")) multiplexer_8 (
    .in0(data[6]), .in1(data[7]), .out(multiplexer_8_out), .sel(not_1_out));
  Multiplexer #(.enable("false")) multiplexer_9 (
    .in0(data[7]), .in1(data[8]), .out(multiplexer_9_out), .sel(not_1_out));
  Multiplexer #(.enable("false")) multiplexer_10 (
    .in0(data[8]), .in1(data[9]), .out(multiplexer_10_out), .sel(not_1_out));
  Multiplexer #(.enable("false")) multiplexer_11 (
    .in0(data[9]), .in1(data[10]), .out(multiplexer_11_out), .sel(not_1_out));
  Multiplexer #(.enable("false")) multiplexer_12 (
    .in0(data[10]), .in1(data[11]), .out(multiplexer_12_out), .sel(not_1_out));
  Multiplexer #(.enable("false")) multiplexer_13 (
    .in0(data[11]), .in1(data[12]), .out(multiplexer_13_out), .sel(not_1_out));
  Multiplexer #(.enable("false")) multiplexer_14 (
    .in0(data[12]), .in1(data[13]), .out(multiplexer_14_out), .sel(not_1_out));
  Multiplexer #(.enable("false")) multiplexer_15 (
    .in0(data[13]), .in1(data[14]), .out(multiplexer_15_out), .sel(not_1_out));
  Multiplexer #(.enable("false")) multiplexer_16 (
    .in0(data[14]), .in1(data[15]), .out(multiplexer_16_out), .sel(not_1_out));
  not not_1 (not_1_out, shiftAmount[0]);
  not not_2 (not_2_out, shiftAmount[1]);
  Multiplexer #(.enable("false")) multiplexer_17 (
    .in0(1'b0), .in1(multiplexer_1_out), .out(multiplexer_17_out), .sel(not_2_out));
  Multiplexer #(.enable("false")) multiplexer_18 (
    .in0(1'b0), .in1(multiplexer_2_out), .out(multiplexer_18_out), .sel(not_2_out));
  Multiplexer #(.enable("false")) multiplexer_19 (
    .in0(multiplexer_1_out), .in1(multiplexer_3_out), .out(multiplexer_19_out), .sel(not_2_out));
  Multiplexer #(.enable("false")) multiplexer_20 (
    .in0(multiplexer_2_out), .in1(multiplexer_4_out), .out(multiplexer_20_out), .sel(not_2_out));
  Multiplexer #(.enable("false")) multiplexer_21 (
    .in0(multiplexer_3_out), .in1(multiplexer_5_out), .out(multiplexer_21_out), .sel(not_2_out));
  Multiplexer #(.enable("false")) multiplexer_22 (
    .in0(multiplexer_4_out), .in1(multiplexer_6_out), .out(multiplexer_22_out), .sel(not_2_out));
  Multiplexer #(.enable("false")) multiplexer_23 (
    .in0(multiplexer_5_out), .in1(multiplexer_7_out), .out(multiplexer_23_out), .sel(not_2_out));
  Multiplexer #(.enable("false")) multiplexer_24 (
    .in0(multiplexer_6_out), .in1(multiplexer_8_out), .out(multiplexer_24_out), .sel(not_2_out));
  Multiplexer #(.enable("false")) multiplexer_25 (
    .in0(multiplexer_7_out), .in1(multiplexer_9_out), .out(multiplexer_25_out), .sel(not_2_out));
  Multiplexer #(.enable("false")) multiplexer_26 (
    .in0(multiplexer_8_out), .in1(multiplexer_10_out), .out(multiplexer_26_out), .sel(not_2_out));
  Multiplexer #(.enable("false")) multiplexer_27 (
    .in0(multiplexer_9_out), .in1(multiplexer_11_out), .out(multiplexer_27_out), .sel(not_2_out));
  Multiplexer #(.enable("false")) multiplexer_28 (
    .in0(multiplexer_10_out), .in1(multiplexer_12_out), .out(multiplexer_28_out), .sel(not_2_out));
  Multiplexer #(.enable("false")) multiplexer_29 (
    .in0(multiplexer_11_out), .in1(multiplexer_13_out), .out(multiplexer_29_out), .sel(not_2_out));
  Multiplexer #(.enable("false")) multiplexer_30 (
    .in0(multiplexer_12_out), .in1(multiplexer_14_out), .out(multiplexer_30_out), .sel(not_2_out));
  Multiplexer #(.enable("false")) multiplexer_31 (
    .in0(multiplexer_13_out), .in1(multiplexer_15_out), .out(multiplexer_31_out), .sel(not_2_out));
  Multiplexer #(.enable("false")) multiplexer_32 (
    .in0(multiplexer_14_out), .in1(multiplexer_16_out), .out(multiplexer_32_out), .sel(not_2_out));
  Multiplexer #(.enable("false")) multiplexer_33 (
    .in0(1'b0), .in1(multiplexer_17_out), .out(shifted[0]), .sel(not_3_out));
  Multiplexer #(.enable("false")) multiplexer_34 (
    .in0(1'b0), .in1(multiplexer_18_out), .out(shifted[1]), .sel(not_3_out));
  Multiplexer #(.enable("false")) multiplexer_35 (
    .in0(1'b0), .in1(multiplexer_19_out), .out(shifted[2]), .sel(not_3_out));
  Multiplexer #(.enable("false")) multiplexer_36 (
    .in0(1'b0), .in1(multiplexer_20_out), .out(shifted[3]), .sel(not_3_out));
  Multiplexer #(.enable("false")) multiplexer_37 (
    .in0(multiplexer_17_out), .in1(multiplexer_21_out), .out(shifted[4]), .sel(not_3_out));
  Multiplexer #(.enable("false")) multiplexer_38 (
    .in0(multiplexer_18_out), .in1(multiplexer_22_out), .out(shifted[5]), .sel(not_3_out));
  Multiplexer #(.enable("false")) multiplexer_39 (
    .in0(multiplexer_19_out), .in1(multiplexer_23_out), .out(shifted[6]), .sel(not_3_out));
  Multiplexer #(.enable("false")) multiplexer_40 (
    .in0(multiplexer_20_out), .in1(multiplexer_24_out), .out(shifted[7]), .sel(not_3_out));
  Multiplexer #(.enable("false")) multiplexer_41 (
    .in0(multiplexer_21_out), .in1(multiplexer_25_out), .out(shifted[8]), .sel(not_3_out));
  Multiplexer #(.enable("false")) multiplexer_42 (
    .in0(multiplexer_22_out), .in1(multiplexer_26_out), .out(shifted[9]), .sel(not_3_out));
  Multiplexer #(.enable("false")) multiplexer_43 (
    .in0(multiplexer_23_out), .in1(multiplexer_27_out), .out(shifted[10]), .sel(not_3_out));
  Multiplexer #(.enable("false")) multiplexer_44 (
    .in0(multiplexer_24_out), .in1(multiplexer_28_out), .out(shifted[11]), .sel(not_3_out));
  Multiplexer #(.enable("false")) multiplexer_45 (
    .in0(multiplexer_25_out), .in1(multiplexer_29_out), .out(shifted[12]), .sel(not_3_out));
  Multiplexer #(.enable("false")) multiplexer_46 (
    .in0(multiplexer_26_out), .in1(multiplexer_30_out), .out(shifted[13]), .sel(not_3_out));
  Multiplexer #(.enable("false")) multiplexer_47 (
    .in0(multiplexer_27_out), .in1(multiplexer_31_out), .out(shifted[14]), .sel(not_3_out));
  Multiplexer #(.enable("false")) multiplexer_48 (
    .in0(multiplexer_28_out), .in1(multiplexer_32_out), .out(shifted[15]), .sel(not_3_out));
  not not_3 (not_3_out, shiftAmount[2]);
endmodule

module rightShift (
  input  [15:0] data,
  input  [2:0] shiftAmount,
  output [15:0] out_3
);

  leftShift leftshift_1 (
    .data({data[0], data[1], data[2], data[3], data[4], data[5], data[6], data[7], data[8], data[9], data[10], data[11], data[12], data[13], data[14], data[15]}),
    .shiftAmount(shiftAmount),
    .shifted({out_3[0], out_3[1], out_3[2], out_3[3], out_3[4], out_3[5], out_3[6], out_3[7], out_3[8], out_3[9], out_3[10], out_3[11], out_3[12], out_3[13], out_3[14], out_3[15]}));
endmodule

module memory_latch (
  input  [15:0] address,
  input  WE,
  input  clk,
  input  [15:0] data_in,
  output [15:0] address_latched,
  output WE_latched,
  output OE_latched,
  output [15:0] data_in_latched
);

  wire DMwe_latch_q;
  wire [15:0] addr_latch_q;

  Register #(.width(16), .trigger("falling")) addr_latch (
    .D(address), .en(WE), .clk(clk), .Q(addr_latch_q));  // open: clr
  D_Flip_Flop #(.trigger("falling")) DMwe_latch (.D(WE), .clk(clk), .Q(DMwe_latch_q));  // open: Qn, preset, reset
  Register #(.width(16), .trigger("falling")) data_to_be_written (
    .D(data_in), .en(WE), .clk(clk), .Q(data_in_latched));  // open: clr
  Multiplexer #(.width(16), .enable("false")) multiplexer_1 (
    .in0(address), .in1(addr_latch_q), .out(address_latched), .sel(DMwe_latch_q));
  and and_1 (WE_latched, clk, DMwe_latch_q);
  not not_1 (OE_latched, WE_latched);
endmodule
