// Logisim project my_adder.circ as structural Verilog: 3 circuits, main circuit main
module main (
  input  [15:0] A,
  input  [15:0] B,
  input  sub,
  output [15:0] result,
  output ovf
);

  wire cir_1_ovf, cir_2_ovf, cir_3_ovf, cir_4_ovf, cir_5_ovf, cir_6_ovf, cir_7_ovf, cir_8_ovf, cir_9_ovf,
       cir_10_ovf, cir_11_ovf, cir_12_ovf, cir_13_ovf, cir_14_ovf, cir_15_ovf, cir_16_ovf, xor_1_out,
       xor_2_out, xor_3_out, xor_4_out, xor_5_out, xor_6_out, xor_7_out, xor_8_out, xor_9_out, xor_10_out,
       xor_11_out, xor_12_out, xor_13_out, xor_14_out, xor_15_out, xor_16_out;

  xor xor_1 (xor_1_out, B[0], sub);
  xor xor_2 (xor_2_out, B[1], sub);
  xor xor_3 (xor_3_out, B[2], sub);
  xor xor_4 (xor_4_out, B[3], sub);
  xor xor_5 (xor_5_out, B[4], sub);
  xor xor_6 (xor_6_out, B[5], sub);
  xor xor_7 (xor_7_out, B[6], sub);
  xor xor_8 (xor_8_out, B[7], sub);
  xor xor_9 (xor_9_out, B[8], sub);
  xor xor_10 (xor_10_out, B[9], sub);
  xor xor_11 (xor_11_out, B[10], sub);
  xor xor_12 (xor_12_out, B[11], sub);
  xor xor_13 (xor_13_out, B[12], sub);
  xor xor_14 (xor_14_out, B[13], sub);
  xor xor_15 (xor_15_out, B[14], sub);
  xor xor_16 (xor_16_out, B[15], sub);
  cir cir_1 (.A(A[0]), .B(xor_1_out), .carryin(sub), .result(result[0]), .ovf(cir_1_ovf));
  cir cir_2 (.A(A[1]), .B(xor_2_out), .carryin(cir_1_ovf), .result(result[1]), .ovf(cir_2_ovf));
  cir cir_3 (.A(A[2]), .B(xor_3_out), .carryin(cir_2_ovf), .result(result[2]), .ovf(cir_3_ovf));
  cir cir_4 (.A(A[3]), .B(xor_4_out), .carryin(cir_3_ovf), .result(result[3]), .ovf(cir_4_ovf));
  cir cir_5 (.A(A[4]), .B(xor_5_out), .carryin(cir_4_ovf), .result(result[4]), .ovf(cir_5_ovf));
  cir cir_6 (.A(A[5]), .B(xor_6_out), .carryin(cir_5_ovf), .result(result[5]), .ovf(cir_6_ovf));
  cir cir_7 (.A(A[6]), .B(xor_7_out), .carryin(cir_6_ovf), .result(result[6]), .ovf(cir_7_ovf));
  cir cir_8 (.A(A[7]), .B(xor_8_out), .carryin(cir_7_ovf), .result(result[7]), .ovf(cir_8_ovf));
  cir cir_9 (.A(A[8]), .B(xor_9_out), .carryin(cir_8_ovf), .result(result[8]), .ovf(cir_9_ovf));
  cir cir_10 (.A(A[9]), .B(xor_10_out), .carryin(cir_9_ovf), .result(result[9]), .ovf(cir_10_ovf));
  cir cir_11 (.A(A[10]), .B(xor_11_out), .carryin(cir_10_ovf), .result(result[10]), .ovf(cir_11_ovf));
  cir cir_12 (.A(A[11]), .B(xor_12_out), .carryin(cir_11_ovf), .result(result[11]), .ovf(cir_12_ovf));
  cir cir_13 (.A(A[12]), .B(xor_13_out), .carryin(cir_12_ovf), .result(result[12]), .ovf(cir_13_ovf));
  cir cir_14 (.A(A[13]), .B(xor_14_out), .carryin(cir_13_ovf), .result(result[13]), .ovf(cir_14_ovf));
  cir cir_15 (.A(A[14]), .B(xor_15_out), .carryin(cir_14_ovf), .result(result[14]), .ovf(cir_15_ovf));
  cir cir_16 (.A(A[15]), .B(xor_16_out), .carryin(cir_15_ovf), .result(result[15]), .ovf(cir_16_ovf));
  xor xor_17 (ovf, cir_15_ovf, cir_16_ovf);

  // Other names for the same wires on the sheet: a1 = A[0]; a2 = A[1]; a3 = A[2]; a4 = A[3]; a5 = A[4]; a6 = A[5];
  //   a7 = A[6]; a8 = A[7]; a9 = A[8]; a10 = A[9]; a11 = A[10]; a12 = A[11]; a13 = A[12]; a14 = A[13]; a15 = A[14];
  //   a16 = A[15]; b1 = B[0]; b2 = B[1]; b3 = B[2]; b4 = B[3]; b5 = B[4]; b6 = B[5]; b7 = B[6]; b8 = B[7]; b9 = B[8];
  //   b10 = B[9]; b11 = B[10]; b12 = B[11]; b13 = B[12]; b14 = B[13]; b15 = B[14]; b16 = B[15]
endmodule

module fulladd (
  input  [15:0] in_1,
  input  [15:0] in_2,
  input  in_3,
  output [15:0] out_4,
  output out_5
);

  wire cir_1_ovf, cir_2_ovf, cir_3_ovf, cir_4_ovf, cir_5_ovf, cir_6_ovf, cir_7_ovf, cir_8_ovf, cir_9_ovf,
       cir_10_ovf, cir_11_ovf, cir_12_ovf, cir_13_ovf, cir_14_ovf, cir_15_ovf, cir_16_ovf, xor_1_out,
       xor_2_out, xor_3_out, xor_4_out, xor_5_out, xor_6_out, xor_7_out, xor_8_out, xor_9_out, xor_10_out,
       xor_11_out, xor_12_out, xor_13_out, xor_14_out, xor_15_out, xor_16_out;

  xor xor_1 (xor_1_out, in_2[0], in_3);
  xor xor_2 (xor_2_out, in_2[1], in_3);
  xor xor_3 (xor_3_out, in_2[2], in_3);
  xor xor_4 (xor_4_out, in_2[3], in_3);
  xor xor_5 (xor_5_out, in_2[4], in_3);
  xor xor_6 (xor_6_out, in_2[5], in_3);
  xor xor_7 (xor_7_out, in_2[6], in_3);
  xor xor_8 (xor_8_out, in_2[7], in_3);
  xor xor_9 (xor_9_out, in_2[8], in_3);
  xor xor_10 (xor_10_out, in_2[9], in_3);
  xor xor_11 (xor_11_out, in_2[10], in_3);
  xor xor_12 (xor_12_out, in_2[11], in_3);
  xor xor_13 (xor_13_out, in_2[12], in_3);
  xor xor_14 (xor_14_out, in_2[13], in_3);
  xor xor_15 (xor_15_out, in_2[14], in_3);
  xor xor_16 (xor_16_out, in_2[15], in_3);
  cir cir_1 (.A(in_1[0]), .B(xor_1_out), .carryin(in_3), .result(out_4[0]), .ovf(cir_1_ovf));
  cir cir_2 (.A(in_1[1]), .B(xor_2_out), .carryin(cir_1_ovf), .result(out_4[1]), .ovf(cir_2_ovf));
  cir cir_3 (.A(in_1[2]), .B(xor_3_out), .carryin(cir_2_ovf), .result(out_4[2]), .ovf(cir_3_ovf));
  cir cir_4 (.A(in_1[3]), .B(xor_4_out), .carryin(cir_3_ovf), .result(out_4[3]), .ovf(cir_4_ovf));
  cir cir_5 (.A(in_1[4]), .B(xor_5_out), .carryin(cir_4_ovf), .result(out_4[4]), .ovf(cir_5_ovf));
  cir cir_6 (.A(in_1[5]), .B(xor_6_out), .carryin(cir_5_ovf), .result(out_4[5]), .ovf(cir_6_ovf));
  cir cir_7 (.A(in_1[6]), .B(xor_7_out), .carryin(cir_6_ovf), .result(out_4[6]), .ovf(cir_7_ovf));
  cir cir_8 (.A(in_1[7]), .B(xor_8_out), .carryin(cir_7_ovf), .result(out_4[7]), .ovf(cir_8_ovf));
  cir cir_9 (.A(in_1[8]), .B(xor_9_out), .carryin(cir_8_ovf), .result(out_4[8]), .ovf(cir_9_ovf));
  cir cir_10 (.A(in_1[9]), .B(xor_10_out), .carryin(cir_9_ovf), .result(out_4[9]), .ovf(cir_10_ovf));
  cir cir_11 (.A(in_1[10]), .B(xor_11_out), .carryin(cir_10_ovf), .result(out_4[10]), .ovf(cir_11_ovf));
  cir cir_12 (.A(in_1[11]), .B(xor_12_out), .carryin(cir_11_ovf), .result(out_4[11]), .ovf(cir_12_ovf));
  cir cir_13 (.A(in_1[12]), .B(xor_13_out), .carryin(cir_12_ovf), .result(out_4[12]), .ovf(cir_13_ovf));
  cir cir_14 (.A(in_1[13]), .B(xor_14_out), .carryin(cir_13_ovf), .result(out_4[13]), .ovf(cir_14_ovf));
  cir cir_15 (.A(in_1[14]), .B(xor_15_out), .carryin(cir_14_ovf), .result(out_4[14]), .ovf(cir_15_ovf));
  cir cir_16 (.A(in_1[15]), .B(xor_16_out), .carryin(cir_15_ovf), .result(out_4[15]), .ovf(cir_16_ovf));
  xor xor_17 (out_5, cir_15_ovf, cir_16_ovf);

  // Other names for the same wires on the sheet: a1 = in_1[0]; a2 = in_1[1]; a3 = in_1[2]; a4 = in_1[3]; a5 = in_1[4];
  //   a6 = in_1[5]; a7 = in_1[6]; a8 = in_1[7]; a9 = in_1[8]; a10 = in_1[9]; a11 = in_1[10]; a12 = in_1[11];
  //   a13 = in_1[12]; a14 = in_1[13]; a15 = in_1[14]; a16 = in_1[15]; b1 = in_2[0]; b2 = in_2[1]; b3 = in_2[2];
  //   b4 = in_2[3]; b5 = in_2[4]; b6 = in_2[5]; b7 = in_2[6]; b8 = in_2[7]; b9 = in_2[8]; b10 = in_2[9];
  //   b11 = in_2[10]; b12 = in_2[11]; b13 = in_2[12]; b14 = in_2[13]; b15 = in_2[14]; b16 = in_2[15]
endmodule

module cir (
  input  A,
  input  B,
  input  carryin,
  output result,
  output ovf
);

  wire and_1_out, and_2_out, xor_1_out;

  and and_1 (and_1_out, B, A);
  xor xor_1 (xor_1_out, A, B);
  or or_1 (ovf, and_1_out, and_2_out);
  and and_2 (and_2_out, xor_1_out, carryin);
  xor xor_2 (result, carryin, xor_1_out);

  // Other names for the same wires on the sheet: cy = carryin
endmodule
