// Logisim project registerFile.circ as structural Verilog: 2 circuits, main circuit singlereg
module singlereg (
  input  [15:0] datain,
  input  clk,
  input  writeEnable,
  input  reset,
  output [15:0] dataout
);

  wire clk_t;

  and and_1 (clk_t, clk, writeEnable);
  D_Flip_Flop d_ff_1 (.D(datain[0]), .clk(clk_t), .Q(dataout[0]), .reset(reset));  // open: Qn, preset
  D_Flip_Flop d_ff_2 (.D(datain[1]), .clk(clk_t), .Q(dataout[1]), .reset(reset));  // open: Qn, preset
  D_Flip_Flop d_ff_3 (.D(datain[2]), .clk(clk_t), .Q(dataout[2]), .reset(reset));  // open: Qn, preset
  D_Flip_Flop d_ff_4 (.D(datain[3]), .clk(clk_t), .Q(dataout[3]), .reset(reset));  // open: Qn, preset
  D_Flip_Flop d_ff_5 (.D(datain[4]), .clk(clk_t), .Q(dataout[4]), .reset(reset));  // open: Qn, preset
  D_Flip_Flop d_ff_6 (.D(datain[5]), .clk(clk_t), .Q(dataout[5]), .reset(reset));  // open: Qn, preset
  D_Flip_Flop d_ff_7 (.D(datain[6]), .clk(clk_t), .Q(dataout[6]), .reset(reset));  // open: Qn, preset
  D_Flip_Flop d_ff_8 (.D(datain[7]), .clk(clk_t), .Q(dataout[7]), .reset(reset));  // open: Qn, preset
  D_Flip_Flop d_ff_9 (.D(datain[8]), .clk(clk_t), .Q(dataout[8]), .reset(reset));  // open: Qn, preset
  D_Flip_Flop d_ff_10 (.D(datain[9]), .clk(clk_t), .Q(dataout[9]), .reset(reset));  // open: Qn, preset
  D_Flip_Flop d_ff_11 (.D(datain[10]), .clk(clk_t), .Q(dataout[10]), .reset(reset));  // open: Qn, preset
  D_Flip_Flop d_ff_12 (.D(datain[11]), .clk(clk_t), .Q(dataout[11]), .reset(reset));  // open: Qn, preset
  D_Flip_Flop d_ff_13 (.D(datain[12]), .clk(clk_t), .Q(dataout[12]), .reset(reset));  // open: Qn, preset
  D_Flip_Flop d_ff_14 (.D(datain[13]), .clk(clk_t), .Q(dataout[13]), .reset(reset));  // open: Qn, preset
  D_Flip_Flop d_ff_15 (.D(datain[14]), .clk(clk_t), .Q(dataout[14]), .reset(reset));  // open: Qn, preset
  D_Flip_Flop d_ff_16 (.D(datain[15]), .clk(clk_t), .Q(dataout[15]), .reset(reset));  // open: Qn, preset

  // Other names for the same wires on the sheet: in0 = datain[0]; in1 = datain[1]; in2 = datain[2]; in3 = datain[3];
  //   in4 = datain[4]; in5 = datain[5]; in6 = datain[6]; in7 = datain[7]; in8 = datain[8]; in9 = datain[9];
  //   in10 = datain[10]; in11 = datain[11]; in12 = datain[12]; in13 = datain[13]; in14 = datain[14];
  //   in15 = datain[15]; o0 = dataout[0]; o1 = dataout[1]; o2 = dataout[2]; o3 = dataout[3]; o4 = dataout[4];
  //   o5 = dataout[5]; o6 = dataout[6]; o7 = dataout[7]; o8 = dataout[8]; o9 = dataout[9]; o10 = dataout[10];
  //   o11 = dataout[11]; o12 = dataout[12]; o13 = dataout[13]; o14 = dataout[14]; o15 = dataout[15]
endmodule

module regfile (
  input  clk,
  input  Reset,
  input  [15:0] writeData,
  input  [2:0] ReadReg1,
  input  [2:0] ReadReg2,
  input  [2:0] WriteReg,
  input  RegWriteEnable,
  output [15:0] ReadData1,
  output [15:0] ReadData2
);

  wire a0, a1, a2, a3, a4, a5, a6, a7, decoder_1_out0, decoder_1_out1, decoder_1_out2, decoder_1_out3,
       decoder_1_out4, decoder_1_out5, decoder_1_out6, decoder_1_out7, w0, w1, w2, w3, w4, w5, w6, w7;
  wire [15:0] singlereg_1_dataout, singlereg_2_dataout, singlereg_3_dataout, singlereg_4_dataout,
       singlereg_5_dataout, singlereg_6_dataout, singlereg_7_dataout;

  Decoder #(.select(3)) decoder_1 (
    .out0(decoder_1_out0), .out1(decoder_1_out1), .out2(decoder_1_out2), .out3(decoder_1_out3),
    .out4(decoder_1_out4), .out5(decoder_1_out5), .out6(decoder_1_out6), .out7(decoder_1_out7), .sel(ReadReg1));  // open: en
  Decoder #(.select(3)) decoder_2 (
    .out0(a0), .out1(a1), .out2(a2), .out3(a3), .out4(a4), .out5(a5), .out6(a6), .out7(a7), .sel(ReadReg2));  // open: en
  Decoder #(.select(3)) decoder_3 (
    .out0(w0), .out1(w1), .out2(w2), .out3(w3), .out4(w4), .out5(w5), .out6(w6), .out7(w7), .sel(WriteReg),
    .en(RegWriteEnable));
  assign ReadData2 = a0 ? {16{1'b0}} : 16'bz;  // Controlled_Buffer controlled_buffer_1
  singlereg singlereg_1 (.datain(writeData), .clk(clk), .writeEnable(w1), .reset(Reset), .dataout(singlereg_1_dataout));
  singlereg singlereg_2 (.datain(writeData), .clk(clk), .writeEnable(w2), .reset(Reset), .dataout(singlereg_2_dataout));
  singlereg singlereg_3 (.datain(writeData), .clk(clk), .writeEnable(w3), .reset(Reset), .dataout(singlereg_3_dataout));
  singlereg singlereg_4 (.datain(writeData), .clk(clk), .writeEnable(w4), .reset(Reset), .dataout(singlereg_4_dataout));
  singlereg singlereg_5 (.datain(writeData), .clk(clk), .writeEnable(w5), .reset(Reset), .dataout(singlereg_5_dataout));
  singlereg singlereg_6 (.datain(writeData), .clk(clk), .writeEnable(w6), .reset(Reset), .dataout(singlereg_6_dataout));
  singlereg singlereg_7 (.datain(writeData), .clk(clk), .writeEnable(w7), .reset(Reset), .dataout(singlereg_7_dataout));
  assign ReadData1 = decoder_1_out0 ? {16{1'b0}} : 16'bz;  // Controlled_Buffer controlled_buffer_2
  assign ReadData2 = a1 ? singlereg_1_dataout : 16'bz;  // Controlled_Buffer controlled_buffer_3
  assign ReadData1 = decoder_1_out1 ? singlereg_1_dataout : 16'bz;  // Controlled_Buffer controlled_buffer_4
  assign ReadData2 = a2 ? singlereg_2_dataout : 16'bz;  // Controlled_Buffer controlled_buffer_5
  assign ReadData1 = decoder_1_out2 ? singlereg_2_dataout : 16'bz;  // Controlled_Buffer controlled_buffer_6
  assign ReadData2 = a3 ? singlereg_3_dataout : 16'bz;  // Controlled_Buffer controlled_buffer_7
  assign ReadData1 = decoder_1_out3 ? singlereg_3_dataout : 16'bz;  // Controlled_Buffer controlled_buffer_8
  assign ReadData2 = a4 ? singlereg_4_dataout : 16'bz;  // Controlled_Buffer controlled_buffer_9
  assign ReadData1 = decoder_1_out4 ? singlereg_4_dataout : 16'bz;  // Controlled_Buffer controlled_buffer_10
  assign ReadData2 = a5 ? singlereg_5_dataout : 16'bz;  // Controlled_Buffer controlled_buffer_11
  assign ReadData1 = decoder_1_out5 ? singlereg_5_dataout : 16'bz;  // Controlled_Buffer controlled_buffer_12
  assign ReadData2 = a6 ? singlereg_6_dataout : 16'bz;  // Controlled_Buffer controlled_buffer_13
  assign ReadData1 = decoder_1_out6 ? singlereg_6_dataout : 16'bz;  // Controlled_Buffer controlled_buffer_14
  assign ReadData2 = a7 ? singlereg_7_dataout : 16'bz;  // Controlled_Buffer controlled_buffer_15
  assign ReadData1 = decoder_1_out7 ? singlereg_7_dataout : 16'bz;  // Controlled_Buffer controlled_buffer_16

  // Other names for the same wires on the sheet: d0[15:0] = ReadData2; d1[15:0] = ReadData2; d2[15:0] = ReadData2;
  //   d3[15:0] = ReadData2; d4[15:0] = ReadData2; d5[15:0] = ReadData2; d6[15:0] = ReadData2; d7[15:0] = ReadData2;
  //   wD[15:0] = writeData
endmodule
