// Logisim project shifter.circ as structural Verilog: 22 circuits, main circuit oneregister
module main (
  input  reset
);

  wire addi_control, alu_1_p3, alu_2_p1, BTL, clk, EQz, keyboard_1_avail, KEYEN, memory_latch_1_oe_latched,
       memory_latch_1_we_latched, memWriteEn, not_1_out, not_3_out, or_1_out, regWriteEn, reset_t, TTYEN;
  wire [2:0] ALUop, rd_writeReg, rs_read2, rt_read1, shamt, undriven, undriven_2, undriven_3, undriven_4,
       undriven_5, undriven_6, write_address;
  wire [3:0] opCode;
  wire [5:0] immediate;
  wire [6:0] bit_extender_2_out, keyboard_1_data;
  wire [14:0] add_sub_1_result;
  wire [15:0] ALUout, B, bit_extender_1_out, currentPC, immediate16, instruction, KeyOut, L,
       memory_latch_1_address_latched, memory_latch_1_data_in_latched, memoryData, multiplexer_7_out,
       next_pc, NextPC_BEQ, NextPC_BLT, PCplus1, RS, RT, undriven_7, undriven_8, undriven_9, undriven_10,
       undriven_11, undriven_12, write_data;

  Clock clock_1 (.out(clk));
  not not_1 (not_1_out, clk);
  opCodeControl opcodecontrol_1 (
    .opCode(opCode), .addi_control(addi_control), .alu_digit3(ALUop[2]), .alu_digit2(ALUop[1]),
    .alu_digit1(ALUop[0]), .memWriteEn(memWriteEn), .regWriteEn(regWriteEn), .screenEn(TTYEN), .KEYEN(KEYEN));
  or or_1 (or_1_out, RS[0], RS[1], RS[2], RS[3], RS[4], RS[5], RS[6], RS[7], RS[8], RS[9], RS[10], RS[11], RS[12], RS[13], RS[14], RS[15]);
  add_sub add_sub_1 (.sub(1'b1), .A(RS), .B(RT), .result({BTL, add_sub_1_result}));  // open: ovf
  register1 register1_1 (.regIn(next_pc), .reset(reset_t), .WE(1'b1), .clk(not_1_out), .regOut(currentPC));
  Format format_1 (
    .instruction(instruction), .shamt(shamt), .rd_writeReg(rd_writeReg), .rt_read1(rt_read1),
    .rs_read2(rs_read2), .immediate(immediate), .jAddress(L), .opCode(opCode));
  not not_2 (EQz, or_1_out);
  // ALU alu_1: pin names not known; wires that end beside it: PCplus1, immediate16, alu_1_p3, B
  Keyboard keyboard_1 (.clk(clk), .re(KEYEN), .clr(reset_t), .avail(keyboard_1_avail), .data(keyboard_1_data));
  ROM #(.addrWidth(16), .dataWidth(16)) rom_1 (.addr(currentPC), .data(instruction));
  // Probe on 16'h80
  Multiplexer #(.width(16), .enable("false")) multiplexer_1 (
    .in0(16'h80), .in1(bit_extender_1_out), .out(KeyOut), .sel(keyboard_1_avail));
  assign bit_extender_1_out = {{9{1'b0}}, keyboard_1_data};  // Bit_Extender bit_extender_1
  Multiplexer #(.width(16), .enable("false")) multiplexer_2 (.in0(PCplus1), .in1(B), .out(NextPC_BEQ), .sel(EQz));
  Multiplexer #(.width(16), .enable("false")) multiplexer_3 (.in0(PCplus1), .in1(B), .out(NextPC_BLT), .sel(BTL));
  // ALU alu_2: pin names not known; wires that end beside it: alu_2_p1, alu_2_p1, currentPC, 16'h1, 3'b000, PCplus1
  Bit_Extender #(.in_width(16), .out_width(7)) bit_extender_2 (.in(RS), .out(bit_extender_2_out));
  TTY #(.rows(13), .cols(80)) tty_1 (.data(bit_extender_2_out), .clk(clk), .we(TTYEN), .clr(reset_t));
  Multiplexer #(.select(4), .width(3), .enable("false")) multiplexer_4 (
    .in0(rd_writeReg), .in1(rd_writeReg), .in2(rt_read1), .in3(rd_writeReg), .in4(rd_writeReg),
    .in5(rd_writeReg), .in6(rd_writeReg), .in7(rt_read1), .in8(undriven), .in9(undriven_2),
    .in10(undriven_3), .in11(undriven_4), .in12(undriven_5), .in13(3'b111), .in14(rd_writeReg),
    .in15(undriven_6), .out(write_address), .sel(opCode));
  Multiplexer #(.select(4), .width(16), .enable("false")) multiplexer_5 (
    .in0(ALUout), .in1(ALUout), .in2(ALUout), .in3(ALUout), .in4(ALUout), .in5(ALUout), .in6(ALUout),
    .in7(memoryData), .in8(undriven_7), .in9(undriven_8), .in10(undriven_9), .in11(undriven_10),
    .in12(undriven_11), .in13(PCplus1), .in14(KeyOut), .in15(undriven_12), .out(write_data), .sel(opCode));
  Multiplexer #(.select(4), .width(16), .enable("false")) multiplexer_6 (
    .in0(PCplus1), .in1(PCplus1), .in2(PCplus1), .in3(PCplus1), .in4(PCplus1), .in5(PCplus1), .in6(PCplus1),
    .in7(PCplus1), .in8(PCplus1), .in9(NextPC_BEQ), .in10(NextPC_BLT), .in11(L), .in12(RS), .in13(L),
    .in14(PCplus1), .in15(PCplus1), .out(next_pc), .sel(opCode));
  not not_3 (not_3_out, clk);
  // registerfile registerfile_1: pin names not known; wires that end beside it: write_data, rs_read2, rt_read1, write_address, regWriteEn, reset_t, clk, RS, RT
  memory_latch memory_latch_1 (
    .address(ALUout), .WE(memWriteEn), .clk(not_3_out), .data_in(RT),
    .address_latched(memory_latch_1_address_latched), .WE_latched(memory_latch_1_we_latched),
    .OE_latched(memory_latch_1_oe_latched), .data_in_latched(memory_latch_1_data_in_latched));
  assign immediate16 = {{10{immediate[5]}}, immediate};  // Bit_Extender bit_extender_3
  RAM #(.addrWidth(16), .dataWidth(16), .trigger("high"), .databus("bibus")) ram_1 (
    .addr(memory_latch_1_address_latched), .we(memory_latch_1_we_latched), .oe(memory_latch_1_oe_latched),
    .din(memory_latch_1_data_in_latched), .dout(memoryData));
  Multiplexer #(.width(16), .enable("false")) multiplexer_7 (
    .in0(RT), .in1(immediate16), .out(multiplexer_7_out), .sel(addi_control));
  // Probe on ALUop
  // ALU alu_3: pin names not known; wires that end beside it: shamt, RS, multiplexer_7_out, ALUop, ALUop, ALUop, ALUout

  // Notes on the sheet:
  //   IF RS < RT
  //   Calculate B = PC + 1 + IMM
  //   BEQZERO
  //   contents of rom_1 (hex, n*v repeats v):
  //   204a e008 22a0 f400 e008 22a0 f400 e008 22a0 f400 903f
  //   RS
  //   RT
endmodule

module oneregister (
  input  [15:0] datain,
  input  clk,
  input  writeEnable,
  input  reset,
  output [15:0] dataout
);

  wire clk_t;

  and and_1 (clk_t, clk, writeEnable);
  D_Flip_Flop d_ff_1 (.D(datain[0]), .clk(clk_t), .Q(dataout[0]), .reset(reset));  // open: Qn, preset
  D_Flip_Flop d_ff_2 (.D(datain[1]), .clk(clk_t), .Q(dataout[1]), .reset(reset));  // open: Qn, preset
  D_Flip_Flop d_ff_3 (.D(datain[2]), .clk(clk_t), .Q(dataout[2]), .reset(reset));  // open: Qn, preset
  D_Flip_Flop d_ff_4 (.D(datain[3]), .clk(clk_t), .Q(dataout[3]), .reset(reset));  // open: Qn, preset
  D_Flip_Flop d_ff_5 (.D(datain[4]), .clk(clk_t), .Q(dataout[4]), .reset(reset));  // open: Qn, preset
  D_Flip_Flop d_ff_6 (.D(datain[5]), .clk(clk_t), .Q(dataout[5]), .reset(reset));  // open: Qn, preset
  D_Flip_Flop d_ff_7 (.D(datain[6]), .clk(clk_t), .Q(dataout[6]), .reset(reset));  // open: Qn, preset
  D_Flip_Flop d_ff_8 (.D(datain[7]), .clk(clk_t), .Q(dataout[7]), .reset(reset));  // open: Qn, preset
  D_Flip_Flop d_ff_9 (.D(datain[8]), .clk(clk_t), .Q(dataout[8]), .reset(reset));  // open: Qn, preset
  D_Flip_Flop d_ff_10 (.D(datain[9]), .clk(clk_t), .Q(dataout[9]), .reset(reset));  // open: Qn, preset
  D_Flip_Flop d_ff_11 (.D(datain[10]), .clk(clk_t), .Q(dataout[10]), .reset(reset));  // open: Qn, preset
  D_Flip_Flop d_ff_12 (.D(datain[11]), .clk(clk_t), .Q(dataout[11]), .reset(reset));  // open: Qn, preset
  D_Flip_Flop d_ff_13 (.D(datain[12]), .clk(clk_t), .Q(dataout[12]), .reset(reset));  // open: Qn, preset
  D_Flip_Flop d_ff_14 (.D(datain[13]), .clk(clk_t), .Q(dataout[13]), .reset(reset));  // open: Qn, preset
  D_Flip_Flop d_ff_15 (.D(datain[14]), .clk(clk_t), .Q(dataout[14]), .reset(reset));  // open: Qn, preset
  D_Flip_Flop d_ff_16 (.D(datain[15]), .clk(clk_t), .Q(dataout[15]), .reset(reset));  // open: Qn, preset

  // Other names for the same wires on the sheet: in0 = datain[0]; in1 = datain[1]; in2 = datain[2]; in3 = datain[3];
  //   in4 = datain[4]; in5 = datain[5]; in6 = datain[6]; in7 = datain[7]; in8 = datain[8]; in9 = datain[9];
  //   in10 = datain[10]; in11 = datain[11]; in12 = datain[12]; in13 = datain[13]; in14 = datain[14];
  //   in15 = datain[15]; o0 = dataout[0]; o1 = dataout[1]; o2 = dataout[2]; o3 = dataout[3]; o4 = dataout[4];
  //   o5 = dataout[5]; o6 = dataout[6]; o7 = dataout[7]; o8 = dataout[8]; o9 = dataout[9]; o10 = dataout[10];
  //   o11 = dataout[11]; o12 = dataout[12]; o13 = dataout[13]; o14 = dataout[14]; o15 = dataout[15]
endmodule

module registerfile (
  input  clk,
  input  Reset,
  input  [15:0] writeData,
  input  [2:0] ReadReg1,
  input  [2:0] ReadReg2,
  input  [2:0] WriteReg,
  input  RegWriteEnable,
  output [15:0] ReadData1,
  output [15:0] ReadData2
);

  wire a0, a1, a2, a3, a4, a5, a6, a7, decoder_1_out0, decoder_1_out1, decoder_1_out2, decoder_1_out3,
       decoder_1_out4, decoder_1_out5, decoder_1_out6, decoder_1_out7, w0, w1, w2, w3, w4, w5, w6, w7;
  wire [15:0] oneregister_1_dataout, oneregister_2_dataout, oneregister_3_dataout, oneregister_4_dataout,
       oneregister_5_dataout, oneregister_6_dataout, oneregister_7_dataout;

  Decoder #(.select(3)) decoder_1 (
    .out0(decoder_1_out0), .out1(decoder_1_out1), .out2(decoder_1_out2), .out3(decoder_1_out3),
    .out4(decoder_1_out4), .out5(decoder_1_out5), .out6(decoder_1_out6), .out7(decoder_1_out7), .sel(ReadReg1));  // open: en
  Decoder #(.select(3)) decoder_2 (
    .out0(a0), .out1(a1), .out2(a2), .out3(a3), .out4(a4), .out5(a5), .out6(a6), .out7(a7), .sel(ReadReg2));  // open: en
  Decoder #(.select(3)) decoder_3 (
    .out0(w0), .out1(w1), .out2(w2), .out3(w3), .out4(w4), .out5(w5), .out6(w6), .out7(w7), .sel(WriteReg),
    .en(RegWriteEnable));
  assign ReadData2 = a0 ? {16{1'b0}} : 16'bz;  // Controlled_Buffer controlled_buffer_1
  oneregister oneregister_1 (
    .datain(writeData), .clk(clk), .writeEnable(w1), .reset(Reset), .dataout(oneregister_1_dataout));
  oneregister oneregister_2 (
    .datain(writeData), .clk(clk), .writeEnable(w2), .reset(Reset), .dataout(oneregister_2_dataout));
  oneregister oneregister_3 (
    .datain(writeData), .clk(clk), .writeEnable(w3), .reset(Reset), .dataout(oneregister_3_dataout));
  oneregister oneregister_4 (
    .datain(writeData), .clk(clk), .writeEnable(w4), .reset(Reset), .dataout(oneregister_4_dataout));
  oneregister oneregister_5 (
    .datain(writeData), .clk(clk), .writeEnable(w5), .reset(Reset), .dataout(oneregister_5_dataout));
  oneregister oneregister_6 (
    .datain(writeData), .clk(clk), .writeEnable(w6), .reset(Reset), .dataout(oneregister_6_dataout));
  oneregister oneregister_7 (
    .datain(writeData), .clk(clk), .writeEnable(w7), .reset(Reset), .dataout(oneregister_7_dataout));
  assign ReadData1 = decoder_1_out0 ? {16{1'b0}} : 16'bz;  // Controlled_Buffer controlled_buffer_2
  assign ReadData2 = a1 ? oneregister_1_dataout : 16'bz;  // Controlled_Buffer controlled_buffer_3
  assign ReadData1 = decoder_1_out1 ? oneregister_1_dataout : 16'bz;  // Controlled_Buffer controlled_buffer_4
  assign ReadData2 = a2 ? oneregister_2_dataout : 16'bz;  // Controlled_Buffer controlled_buffer_5
  assign ReadData1 = decoder_1_out2 ? oneregister_2_dataout : 16'bz;  // Controlled_Buffer controlled_buffer_6
  assign ReadData2 = a3 ? oneregister_3_dataout : 16'bz;  // Controlled_Buffer controlled_buffer_7
  assign ReadData1 = decoder_1_out3 ? oneregister_3_dataout : 16'bz;  // Controlled_Buffer controlled_buffer_8
  assign ReadData2 = a4 ? oneregister_4_dataout : 16'bz;  // Controlled_Buffer controlled_buffer_9
  assign ReadData1 = decoder_1_out4 ? oneregister_4_dataout : 16'bz;  // Controlled_Buffer controlled_buffer_10
  assign ReadData2 = a5 ? oneregister_5_dataout : 16'bz;  // Controlled_Buffer controlled_buffer_11
  assign ReadData1 = decoder_1_out5 ? oneregister_5_dataout : 16'bz;  // Controlled_Buffer controlled_buffer_12
  assign ReadData2 = a6 ? oneregister_6_dataout : 16'bz;  // Controlled_Buffer controlled_buffer_13
  assign ReadData1 = decoder_1_out6 ? oneregister_6_dataout : 16'bz;  // Controlled_Buffer controlled_buffer_14
  assign ReadData2 = a7 ? oneregister_7_dataout : 16'bz;  // Controlled_Buffer controlled_buffer_15
  assign ReadData1 = decoder_1_out7 ? oneregister_7_dataout : 16'bz;  // Controlled_Buffer controlled_buffer_16

  // Other names for the same wires on the sheet: d0[15:0] = ReadData2; d1[15:0] = ReadData2; d2[15:0] = ReadData2;
  //   d3[15:0] = ReadData2; d4[15:0] = ReadData2; d5[15:0] = ReadData2; d6[15:0] = ReadData2; d7[15:0] = ReadData2;
  //   wD[15:0] = writeData
endmodule

module formatter (
  input  [15:0] instruction
);
endmodule

module instructions (
  input  [3:0] opcode,
  output Rwe,
  output out_3,
  output [2:0] out_4,
  output out_5,
  output out_6,
  output out_7,
  output out_8,
  output out_9,
  output out_10,
  output out_11,
  output out_12
);

  wire add, addi, \and , j, jal, \or , shl, shr, sub, subi;

  or or_1 (out_4[2], \and , \or );
  or or_2 (out_4[1], shr, shl);
  Decoder #(.select(4), .enable("false")) decoder_1 (
    .out0(out_6), .out1(out_7), .out2(out_8), .out3(out_9), .out4(\or ), .out5(\and ), .out6(addi),
    .out7(add), .out8(sub), .out9(subi), .out10(shr), .out11(shl), .out12(j), .out13(jal), .out14(out_11),
    .out15(out_12), .sel(opcode));
  or or_3 (out_4[0], shr, subi, sub, \or , out_9, out_8);
  or or_4 (out_10, j, jal);
  or or_5 (out_5, out_6, addi, subi, out_7);
  or or_6 (Rwe, \or , out_6, addi, add, sub, subi, shr, shl, jal, out_12, \and );
  or or_7 (out_3, \or , \and , add, sub, shr, shl, out_12);

  // Other names for the same wires on the sheet: beq = out_8; blt = out_9; input = out_12; lw = out_6;
  //   output = out_11; sw = out_7
endmodule

module instructionDecoder (
  input  [3:0] opcode,
  output Rwe,
  output Rdst,
  output [2:0] ALUOp,
  output ALUinB,
  output Rwd,
  output DMwe,
  output BEQ,
  output BLT,
  output JP,
  output OUTPUT,
  output INPUT
);

  wire add, addi, \and , j, jal, \or , shl, shr, sub, subi;

  or or_1 (ALUOp[2], \and , \or );
  or or_2 (ALUOp[1], shr, shl);
  Decoder #(.select(4), .enable("false")) decoder_1 (
    .out0(Rwd), .out1(DMwe), .out2(BEQ), .out3(BLT), .out4(\or ), .out5(\and ), .out6(addi), .out7(add),
    .out8(sub), .out9(subi), .out10(shr), .out11(shl), .out12(j), .out13(jal), .out14(OUTPUT), .out15(INPUT),
    .sel(opcode));
  or or_3 (ALUOp[0], shr, subi, sub, \or , BLT, BEQ);
  or or_4 (JP, j, jal);
  or or_5 (ALUinB, Rwd, addi, subi, DMwe);
  or or_6 (Rwe, \or , Rwd, addi, add, sub, subi, shr, shl, jal, INPUT, \and );
  or or_7 (Rdst, \or , \and , add, sub, shr, shl, INPUT);

  // Other names for the same wires on the sheet: lw = Rwd; sw = DMwe
endmodule

module ALU (
  input  [15:0] InputData1,
  input  [2:0] OpType,
  input  [15:0] InputData2,
  input  [2:0] Operation,
  input  [2:0] shiftamt,
  output [15:0] OutputData
);

  wire aand, add, adderfull_1_ovf, LShift, oor_t, RShift, sub;
  wire [15:0] OAdder, OAnd, OLeftShift, OOr, ORightShift;

  Decoder #(.select(3)) decoder_1 (
    .out0(add), .out1(sub), .out2(LShift), .out3(RShift), .out4(aand), .out5(oor_t), .sel(Operation));  // open: out6, out7, en
  AdderFull adderfull_1 (.A(InputData1), .B(InputData2), .sub(sub), .result(OAdder), .ovf(adderfull_1_ovf));
  assign OAnd = InputData1 & InputData2;  // AND_Gate and_1, 16 bits wide
  assign OOr = InputData1 | InputData2;  // OR_Gate or_1, 16 bits wide
  threeBitShifterLeft threebitshifterleft_1 (.\input (InputData1), .bits(shiftamt), .\output (OLeftShift));
  threeBitShifterRight threebitshifterright_1 (.\input (InputData1), .bits(shiftamt), .\output (ORightShift));
  Multiplexer #(.select(3), .width(16), .enable("false")) multiplexer_1 (
    .in0(OAdder), .in1(OAdder), .in2(OLeftShift), .in3(ORightShift), .in4(OAnd), .in5(OOr), .out(OutputData),
    .sel(OpType));  // open: in6, in7

  // Other names for the same wires on the sheet: in1[15:0] = InputData1; in2[15:0] = InputData2
endmodule

module oneBitAdder (
  input  A,
  input  B,
  input  carryin,
  output result,
  output ovf
);

  wire and_1_out, and_2_out, xor_1_out;

  and and_1 (and_1_out, B, A);
  xor xor_1 (xor_1_out, A, B);
  or or_1 (ovf, and_1_out, and_2_out);
  and and_2 (and_2_out, xor_1_out, carryin);
  xor xor_2 (result, carryin, xor_1_out);

  // Other names for the same wires on the sheet: cy = carryin
endmodule

module AdderFull (
  input  [15:0] A,
  input  [15:0] B,
  input  sub,
  output [15:0] result,
  output ovf
);

  wire onebitadder_1_ovf, onebitadder_2_ovf, onebitadder_3_ovf, onebitadder_4_ovf, onebitadder_5_ovf,
       onebitadder_6_ovf, onebitadder_7_ovf, onebitadder_8_ovf, onebitadder_9_ovf, onebitadder_10_ovf,
       onebitadder_11_ovf, onebitadder_12_ovf, onebitadder_13_ovf, onebitadder_14_ovf, onebitadder_15_ovf,
       onebitadder_16_ovf, xor_1_out, xor_2_out, xor_3_out, xor_4_out, xor_5_out, xor_6_out, xor_7_out,
       xor_8_out, xor_9_out, xor_10_out, xor_11_out, xor_12_out, xor_13_out, xor_14_out, xor_15_out,
       xor_16_out;

  xor xor_1 (xor_1_out, B[0], sub);
  xor xor_2 (xor_2_out, B[1], sub);
  xor xor_3 (xor_3_out, B[2], sub);
  xor xor_4 (xor_4_out, B[3], sub);
  xor xor_5 (xor_5_out, B[4], sub);
  xor xor_6 (xor_6_out, B[5], sub);
  xor xor_7 (xor_7_out, B[6], sub);
  xor xor_8 (xor_8_out, B[7], sub);
  xor xor_9 (xor_9_out, B[8], sub);
  xor xor_10 (xor_10_out, B[9], sub);
  xor xor_11 (xor_11_out, B[10], sub);
  xor xor_12 (xor_12_out, B[11], sub);
  xor xor_13 (xor_13_out, B[12], sub);
  xor xor_14 (xor_14_out, B[13], sub);
  xor xor_15 (xor_15_out, B[14], sub);
  xor xor_16 (xor_16_out, B[15], sub);
  oneBitAdder onebitadder_1 (.A(A[0]), .B(xor_1_out), .carryin(sub), .result(result[0]), .ovf(onebitadder_1_ovf));
  oneBitAdder onebitadder_2 (
    .A(A[1]), .B(xor_2_out), .carryin(onebitadder_1_ovf), .result(result[1]), .ovf(onebitadder_2_ovf));
  oneBitAdder onebitadder_3 (
    .A(A[2]), .B(xor_3_out), .carryin(onebitadder_2_ovf), .result(result[2]), .ovf(onebitadder_3_ovf));
  oneBitAdder onebitadder_4 (
    .A(A[3]), .B(xor_4_out), .carryin(onebitadder_3_ovf), .result(result[3]), .ovf(onebitadder_4_ovf));
  oneBitAdder onebitadder_5 (
    .A(A[4]), .B(xor_5_out), .carryin(onebitadder_4_ovf), .result(result[4]), .ovf(onebitadder_5_ovf));
  oneBitAdder onebitadder_6 (
    .A(A[5]), .B(xor_6_out), .carryin(onebitadder_5_ovf), .result(result[5]), .ovf(onebitadder_6_ovf));
  oneBitAdder onebitadder_7 (
    .A(A[6]), .B(xor_7_out), .carryin(onebitadder_6_ovf), .result(result[6]), .ovf(onebitadder_7_ovf));
  oneBitAdder onebitadder_8 (
    .A(A[7]), .B(xor_8_out), .carryin(onebitadder_7_ovf), .result(result[7]), .ovf(onebitadder_8_ovf));
  oneBitAdder onebitadder_9 (
    .A(A[8]), .B(xor_9_out), .carryin(onebitadder_8_ovf), .result(result[8]), .ovf(onebitadder_9_ovf));
  oneBitAdder onebitadder_10 (
    .A(A[9]), .B(xor_10_out), .carryin(onebitadder_9_ovf), .result(result[9]), .ovf(onebitadder_10_ovf));
  oneBitAdder onebitadder_11 (
    .A(A[10]), .B(xor_11_out), .carryin(onebitadder_10_ovf), .result(result[10]), .ovf(onebitadder_11_ovf));
  oneBitAdder onebitadder_12 (
    .A(A[11]), .B(xor_12_out), .carryin(onebitadder_11_ovf), .result(result[11]), .ovf(onebitadder_12_ovf));
  oneBitAdder onebitadder_13 (
    .A(A[12]), .B(xor_13_out), .carryin(onebitadder_12_ovf), .result(result[12]), .ovf(onebitadder_13_ovf));
  oneBitAdder onebitadder_14 (
    .A(A[13]), .B(xor_14_out), .carryin(onebitadder_13_ovf), .result(result[13]), .ovf(onebitadder_14_ovf));
  oneBitAdder onebitadder_15 (
    .A(A[14]), .B(xor_15_out), .carryin(onebitadder_14_ovf), .result(result[14]), .ovf(onebitadder_15_ovf));
  oneBitAdder onebitadder_16 (
    .A(A[15]), .B(xor_16_out), .carryin(onebitadder_15_ovf), .result(result[15]), .ovf(onebitadder_16_ovf));
  xor xor_17 (ovf, onebitadder_15_ovf, onebitadder_16_ovf);

  // Other names for the same wires on the sheet: a1 = A[0]; a2 = A[1]; a3 = A[2]; a4 = A[3]; a5 = A[4]; a6 = A[5];
  //   a7 = A[6]; a8 = A[7]; a9 = A[8]; a10 = A[9]; a11 = A[10]; a12 = A[11]; a13 = A[12]; a14 = A[13]; a15 = A[14];
  //   a16 = A[15]; b1 = B[0]; b2 = B[1]; b3 = B[2]; b4 = B[3]; b5 = B[4]; b6 = B[5]; b7 = B[6]; b8 = B[7]; b9 = B[8];
  //   b10 = B[9]; b11 = B[10]; b12 = B[11]; b13 = B[12]; b14 = B[13]; b15 = B[14]; b16 = B[15]
endmodule

module threeBitShifterLeft (
  input  [15:0] \input ,
  input  [2:0] bits,
  output [15:0] \output 
);

  wire [15:0] twobitshifterleft_1_outp;

  twoBitShifterLeft twobitshifterleft_1 (.inp(\input ), .bits(bits[1:0]), .outp(twobitshifterleft_1_outp));
  Multiplexer #(.enable("false")) multiplexer_1 (
    .in0(twobitshifterleft_1_outp[0]), .in1(1'b0), .out(\output [0]), .sel(bits[2]));
  Multiplexer #(.enable("false")) multiplexer_2 (
    .in0(twobitshifterleft_1_outp[1]), .in1(1'b0), .out(\output [1]), .sel(bits[2]));
  Multiplexer #(.enable("false")) multiplexer_3 (
    .in0(twobitshifterleft_1_outp[2]), .in1(1'b0), .out(\output [2]), .sel(bits[2]));
  Multiplexer #(.enable("false")) multiplexer_4 (
    .in0(twobitshifterleft_1_outp[3]), .in1(1'b0), .out(\output [3]), .sel(bits[2]));
  Multiplexer #(.enable("false")) multiplexer_5 (
    .in0(twobitshifterleft_1_outp[4]), .in1(twobitshifterleft_1_outp[0]), .out(\output [4]), .sel(bits[2]));
  Multiplexer #(.enable("false")) multiplexer_6 (
    .in0(twobitshifterleft_1_outp[5]), .in1(twobitshifterleft_1_outp[1]), .out(\output [5]), .sel(bits[2]));
  Multiplexer #(.enable("false")) multiplexer_7 (
    .in0(twobitshifterleft_1_outp[6]), .in1(twobitshifterleft_1_outp[2]), .out(\output [6]), .sel(bits[2]));
  Multiplexer #(.enable("false")) multiplexer_8 (
    .in0(twobitshifterleft_1_outp[7]), .in1(twobitshifterleft_1_outp[3]), .out(\output [7]), .sel(bits[2]));
  Multiplexer #(.enable("false")) multiplexer_9 (
    .in0(twobitshifterleft_1_outp[8]), .in1(twobitshifterleft_1_outp[4]), .out(\output [8]), .sel(bits[2]));
  Multiplexer #(.enable("false")) multiplexer_10 (
    .in0(twobitshifterleft_1_outp[9]), .in1(twobitshifterleft_1_outp[5]), .out(\output [9]), .sel(bits[2]));
  Multiplexer #(.enable("false")) multiplexer_11 (
    .in0(twobitshifterleft_1_outp[10]), .in1(twobitshifterleft_1_outp[6]), .out(\output [10]), .sel(bits[2]));
  Multiplexer #(.enable("false")) multiplexer_12 (
    .in0(twobitshifterleft_1_outp[11]), .in1(twobitshifterleft_1_outp[7]), .out(\output [11]), .sel(bits[2]));
  Multiplexer #(.enable("false")) multiplexer_13 (
    .in0(twobitshifterleft_1_outp[12]), .in1(twobitshifterleft_1_outp[8]), .out(\output [12]), .sel(bits[2]));
  Multiplexer #(.enable("false")) multiplexer_14 (
    .in0(twobitshifterleft_1_outp[13]), .in1(twobitshifterleft_1_outp[9]), .out(\output [13]), .sel(bits[2]));
  Multiplexer #(.enable("false")) multiplexer_15 (
    .in0(twobitshifterleft_1_outp[14]), .in1(twobitshifterleft_1_outp[10]), .out(\output [14]), .sel(bits[2]));
  Multiplexer #(.enable("false")) multiplexer_16 (
    .in0(twobitshifterleft_1_outp[15]), .in1(twobitshifterleft_1_outp[11]), .out(\output [15]), .sel(bits[2]));

  // Other names for the same wires on the sheet: bit0 = bits[0]; bit1 = bits[1]; bit2 = bits[2]; in[15:0] = \input ;
  //   out[15:0] = \output 
endmodule

module twoBitShifterLeft (
  input  [15:0] inp,
  input  [1:0] bits,
  output [15:0] outp
);

  wire [15:0] bitshifterleft_1_outp;

  bitShifterLeft bitshifterleft_1 (.inp(inp), .shift(bits[0]), .outp(bitshifterleft_1_outp));
  Multiplexer #(.enable("false")) multiplexer_1 (
    .in0(bitshifterleft_1_outp[0]), .in1(1'b0), .out(outp[0]), .sel(bits[1]));
  Multiplexer #(.enable("false")) multiplexer_2 (
    .in0(bitshifterleft_1_outp[1]), .in1(1'b0), .out(outp[1]), .sel(bits[1]));
  Multiplexer #(.enable("false")) multiplexer_3 (
    .in0(bitshifterleft_1_outp[2]), .in1(bitshifterleft_1_outp[0]), .out(outp[2]), .sel(bits[1]));
  Multiplexer #(.enable("false")) multiplexer_4 (
    .in0(bitshifterleft_1_outp[3]), .in1(bitshifterleft_1_outp[1]), .out(outp[3]), .sel(bits[1]));
  Multiplexer #(.enable("false")) multiplexer_5 (
    .in0(bitshifterleft_1_outp[4]), .in1(bitshifterleft_1_outp[2]), .out(outp[4]), .sel(bits[1]));
  Multiplexer #(.enable("false")) multiplexer_6 (
    .in0(bitshifterleft_1_outp[5]), .in1(bitshifterleft_1_outp[3]), .out(outp[5]), .sel(bits[1]));
  Multiplexer #(.enable("false")) multiplexer_7 (
    .in0(bitshifterleft_1_outp[6]), .in1(bitshifterleft_1_outp[4]), .out(outp[6]), .sel(bits[1]));
  Multiplexer #(.enable("false")) multiplexer_8 (
    .in0(bitshifterleft_1_outp[7]), .in1(bitshifterleft_1_outp[5]), .out(outp[7]), .sel(bits[1]));
  Multiplexer #(.enable("false")) multiplexer_9 (
    .in0(bitshifterleft_1_outp[8]), .in1(bitshifterleft_1_outp[6]), .out(outp[8]), .sel(bits[1]));
  Multiplexer #(.enable("false")) multiplexer_10 (
    .in0(bitshifterleft_1_outp[9]), .in1(bitshifterleft_1_outp[7]), .out(outp[9]), .sel(bits[1]));
  Multiplexer #(.enable("false")) multiplexer_11 (
    .in0(bitshifterleft_1_outp[10]), .in1(bitshifterleft_1_outp[8]), .out(outp[10]), .sel(bits[1]));
  Multiplexer #(.enable("false")) multiplexer_12 (
    .in0(bitshifterleft_1_outp[11]), .in1(bitshifterleft_1_outp[9]), .out(outp[11]), .sel(bits[1]));
  Multiplexer #(.enable("false")) multiplexer_13 (
    .in0(bitshifterleft_1_outp[12]), .in1(bitshifterleft_1_outp[10]), .out(outp[12]), .sel(bits[1]));
  Multiplexer #(.enable("false")) multiplexer_14 (
    .in0(bitshifterleft_1_outp[13]), .in1(bitshifterleft_1_outp[11]), .out(outp[13]), .sel(bits[1]));
  Multiplexer #(.enable("false")) multiplexer_15 (
    .in0(bitshifterleft_1_outp[14]), .in1(bitshifterleft_1_outp[12]), .out(outp[14]), .sel(bits[1]));
  Multiplexer #(.enable("false")) multiplexer_16 (
    .in0(bitshifterleft_1_outp[15]), .out(outp[15]), .sel(bits[1]));  // open: in1

  // Other names for the same wires on the sheet: bit0 = bits[0]; bit1 = bits[1]; in[15:0] = inp; out[15:0] = outp
endmodule

module bitShifterLeft (
  input  [15:0] inp,
  input  shift,
  output [15:0] outp
);

  Multiplexer #(.enable("false")) multiplexer_1 (.in0(inp[0]), .in1(1'b0), .out(outp[0]), .sel(shift));
  Multiplexer #(.enable("false")) multiplexer_2 (.in0(inp[1]), .in1(inp[0]), .out(outp[1]), .sel(shift));
  Multiplexer #(.enable("false")) multiplexer_3 (.in0(inp[2]), .in1(inp[1]), .out(outp[2]), .sel(shift));
  Multiplexer #(.enable("false")) multiplexer_4 (.in0(inp[3]), .in1(inp[2]), .out(outp[3]), .sel(shift));
  Multiplexer #(.enable("false")) multiplexer_5 (.in0(inp[4]), .in1(inp[3]), .out(outp[4]), .sel(shift));
  Multiplexer #(.enable("false")) multiplexer_6 (.in0(inp[5]), .in1(inp[4]), .out(outp[5]), .sel(shift));
  Multiplexer #(.enable("false")) multiplexer_7 (.in0(inp[6]), .in1(inp[5]), .out(outp[6]), .sel(shift));
  Multiplexer #(.enable("false")) multiplexer_8 (.in0(inp[7]), .in1(inp[6]), .out(outp[7]), .sel(shift));
  Multiplexer #(.enable("false")) multiplexer_9 (.in0(inp[8]), .in1(inp[7]), .out(outp[8]), .sel(shift));
  Multiplexer #(.enable("false")) multiplexer_10 (.in0(inp[9]), .in1(inp[8]), .out(outp[9]), .sel(shift));
  Multiplexer #(.enable("false")) multiplexer_11 (.in0(inp[10]), .in1(inp[9]), .out(outp[10]), .sel(shift));
  Multiplexer #(.enable("false")) multiplexer_12 (.in0(inp[11]), .in1(inp[10]), .out(outp[11]), .sel(shift));
  Multiplexer #(.enable("false")) multiplexer_13 (.in0(inp[12]), .in1(inp[11]), .out(outp[12]), .sel(shift));
  Multiplexer #(.enable("false")) multiplexer_14 (.in0(inp[13]), .in1(inp[12]), .out(outp[13]), .sel(shift));
  Multiplexer #(.enable("false")) multiplexer_15 (.in0(inp[14]), .in1(inp[13]), .out(outp[14]), .sel(shift));
  Multiplexer #(.enable("false")) multiplexer_16 (.in0(inp[15]), .in1(inp[14]), .out(outp[15]), .sel(shift));

  // Other names for the same wires on the sheet: bit0 = shift; in[15:0] = inp; out[15:0] = outp
endmodule

module threeBitShifterRight (
  input  [15:0] \input ,
  input  [2:0] bits,
  output [15:0] \output 
);

  threeBitShifterLeft threebitshifterleft_1 (
    .\input ({\input [0], \input [1], \input [2], \input [3], \input [4], \input [5], \input [6], \input [7], \input [8], \input [9], \input [10], \input [11], \input [12], \input [13], \input [14], \input [15]}),
    .bits(bits),
    .\output ({\output [0], \output [1], \output [2], \output [3], \output [4], \output [5], \output [6], \output [7], \output [8], \output [9], \output [10], \output [11], \output [12], \output [13], \output [14], \output [15]}));
endmodule

module signExtender (
  input  [5:0] \input ,
  output [15:0] \output 
);

  Multiplexer #(.width(10), .enable("false")) multiplexer_1 (
    .in0({10{1'b0}}), .in1({10{1'b1}}), .out(\output [15:6]), .sel(\input [5]));

  assign \output [5:0] = \input ;

  // Other names for the same wires on the sheet: negative = \input [5]
endmodule

module memory_latch (
  input  [15:0] address,
  input  WE,
  input  clk,
  input  [15:0] data_in,
  output [15:0] address_latched,
  output WE_latched,
  output OE_latched,
  output [15:0] data_in_latched
);

  wire DMwe_latch_q;
  wire [15:0] addr_latch_q;

  Register #(.width(16), .trigger("falling")) addr_latch (
    .D(address), .en(WE), .clk(clk), .Q(addr_latch_q));  // open: clr
  D_Flip_Flop #(.trigger("falling")) DMwe_latch (.D(WE), .clk(clk), .Q(DMwe_latch_q));  // open: Qn, preset, reset
  Register #(.width(16), .trigger("falling")) data_to_be_written (
    .D(data_in), .en(WE), .clk(clk), .Q(data_in_latched));  // open: clr
  Multiplexer #(.width(16), .enable("false")) multiplexer_1 (
    .in0(address), .in1(addr_latch_q), .out(address_latched), .sel(DMwe_latch_q));
  and and_1 (WE_latched, clk, DMwe_latch_q);
  not not_1 (OE_latched, WE_latched);
endmodule

module addR (
  input  addA,
  input  addB,
  input  carryIN,
  input  addSub,
  output addSum,
  output carryOUT
);

  wire and_1_out, and_2_out, and_3_out, and_4_out, and_5_out, and_6_out, not_1_out, not_2_out, not_3_out,
       not_4_out, or_2_out, xor_1_out;

  xor xor_1 (xor_1_out, addSub, addA);
  and and_1 (and_1_out, xor_1_out, addB);
  not not_1 (not_1_out, xor_1_out);
  not not_2 (not_2_out, addB);
  or or_1 (carryOUT, and_1_out, and_4_out);
  and and_2 (and_2_out, not_1_out, addB);
  and and_3 (and_3_out, xor_1_out, not_2_out);
  and and_4 (and_4_out, or_2_out, carryIN);
  or or_2 (or_2_out, and_2_out, and_3_out);
  not not_3 (not_3_out, or_2_out);
  not not_4 (not_4_out, carryIN);
  and and_5 (and_5_out, not_3_out, carryIN);
  and and_6 (and_6_out, not_4_out, or_2_out);
  or or_3 (addSum, and_5_out, and_6_out);
endmodule

module add_sub (
  input  sub,
  input  [15:0] A,
  input  [15:0] B,
  output ovf,
  output [15:0] result
);

  wire add1_carryout, add2_carryout, add3_carryout, add4_carryout, add5_carryout, add6_carryout,
       add7_carryout, add8_carryout, add9_carryout, add10_carryout, add11_carryout, add12_carryout,
       add13_carryout, add14_carryout, add15_carryout, add16_carryout;

  addR add1 (.addA(B[0]), .addB(A[0]), .carryIN(sub), .addSub(sub), .addSum(result[0]), .carryOUT(add1_carryout));
  addR add2 (
    .addA(B[1]), .addB(A[1]), .carryIN(add1_carryout), .addSub(sub), .addSum(result[1]),
    .carryOUT(add2_carryout));
  addR add3 (
    .addA(B[2]), .addB(A[2]), .carryIN(add2_carryout), .addSub(sub), .addSum(result[2]),
    .carryOUT(add3_carryout));
  addR add4 (
    .addA(B[3]), .addB(A[3]), .carryIN(add3_carryout), .addSub(sub), .addSum(result[3]),
    .carryOUT(add4_carryout));
  addR add5 (
    .addA(B[4]), .addB(A[4]), .carryIN(add4_carryout), .addSub(sub), .addSum(result[4]),
    .carryOUT(add5_carryout));
  addR add6 (
    .addA(B[5]), .addB(A[5]), .carryIN(add5_carryout), .addSub(sub), .addSum(result[5]),
    .carryOUT(add6_carryout));
  addR add7 (
    .addA(B[6]), .addB(A[6]), .carryIN(add6_carryout), .addSub(sub), .addSum(result[6]),
    .carryOUT(add7_carryout));
  addR add8 (
    .addA(B[7]), .addB(A[7]), .carryIN(add7_carryout), .addSub(sub), .addSum(result[7]),
    .carryOUT(add8_carryout));
  addR add9 (
    .addA(B[8]), .addB(A[8]), .carryIN(add8_carryout), .addSub(sub), .addSum(result[8]),
    .carryOUT(add9_carryout));
  addR add10 (
    .addA(B[9]), .addB(A[9]), .carryIN(add9_carryout), .addSub(sub), .addSum(result[9]),
    .carryOUT(add10_carryout));
  addR add11 (
    .addA(B[10]), .addB(A[10]), .carryIN(add10_carryout), .addSub(sub), .addSum(result[10]),
    .carryOUT(add11_carryout));
  addR add12 (
    .addA(B[11]), .addB(A[11]), .carryIN(add11_carryout), .addSub(sub), .addSum(result[11]),
    .carryOUT(add12_carryout));
  addR add13 (
    .addA(B[12]), .addB(A[12]), .carryIN(add12_carryout), .addSub(sub), .addSum(result[12]),
    .carryOUT(add13_carryout));
  addR add14 (
    .addA(B[13]), .addB(A[13]), .carryIN(add13_carryout), .addSub(sub), .addSum(result[13]),
    .carryOUT(add14_carryout));
  addR add15 (
    .addA(B[14]), .addB(A[14]), .carryIN(add14_carryout), .addSub(sub), .addSum(result[14]),
    .carryOUT(add15_carryout));
  xor xor_1 (ovf, add15_carryout, add16_carryout);
  addR add16 (
    .addA(B[15]), .addB(A[15]), .carryIN(add15_carryout), .addSub(sub), .addSum(result[15]),
    .carryOUT(add16_carryout));
endmodule

module register1 (
  input  [15:0] regIn,
  input  reset,
  input  WE,
  input  clk,
  output [15:0] regOut
);

  wire and_1_out, and_2_out, and_3_out, and_4_out, and_5_out, and_6_out, and_7_out, and_8_out, and_9_out,
       and_10_out, and_11_out, and_12_out, and_13_out, and_14_out, and_15_out, and_16_out;

  D_Flip_Flop d_ff_1 (.D(regIn[0]), .clk(and_1_out), .Q(regOut[0]), .reset(reset));  // open: Qn, preset
  and and_1 (and_1_out, WE, clk);
  and and_2 (and_2_out, WE, clk);
  D_Flip_Flop d_ff_2 (.D(regIn[2]), .clk(and_3_out), .Q(regOut[2]), .reset(reset));  // open: Qn, preset
  and and_3 (and_3_out, WE, clk);
  and and_4 (and_4_out, WE, clk);
  and and_5 (and_5_out, WE, clk);
  and and_6 (and_6_out, WE, clk);
  and and_7 (and_7_out, WE, clk);
  and and_8 (and_8_out, WE, clk);
  and and_9 (and_9_out, WE, clk);
  and and_10 (and_10_out, WE, clk);
  and and_11 (and_11_out, WE, clk);
  and and_12 (and_12_out, WE, clk);
  and and_13 (and_13_out, WE, clk);
  and and_14 (and_14_out, WE, clk);
  D_Flip_Flop d_ff_3 (.D(regIn[1]), .clk(and_2_out), .Q(regOut[1]), .reset(reset));  // open: Qn, preset
  D_Flip_Flop d_ff_4 (.D(regIn[3]), .clk(and_4_out), .Q(regOut[3]), .reset(reset));  // open: Qn, preset
  D_Flip_Flop d_ff_5 (.D(regIn[4]), .clk(and_5_out), .Q(regOut[4]), .reset(reset));  // open: Qn, preset
  D_Flip_Flop d_ff_6 (.D(regIn[5]), .clk(and_6_out), .Q(regOut[5]), .reset(reset));  // open: Qn, preset
  D_Flip_Flop d_ff_7 (.D(regIn[6]), .clk(and_7_out), .Q(regOut[6]), .reset(reset));  // open: Qn, preset
  D_Flip_Flop d_ff_8 (.D(regIn[7]), .clk(and_8_out), .Q(regOut[7]), .reset(reset));  // open: Qn, preset
  D_Flip_Flop d_ff_9 (.D(regIn[8]), .clk(and_9_out), .Q(regOut[8]), .reset(reset));  // open: Qn, preset
  D_Flip_Flop d_ff_10 (.D(regIn[9]), .clk(and_10_out), .Q(regOut[9]), .reset(reset));  // open: Qn, preset
  D_Flip_Flop d_ff_11 (.D(regIn[10]), .clk(and_11_out), .Q(regOut[10]), .reset(reset));  // open: Qn, preset
  D_Flip_Flop d_ff_12 (.D(regIn[11]), .clk(and_12_out), .Q(regOut[11]), .reset(reset));  // open: Qn, preset
  D_Flip_Flop d_ff_13 (.D(regIn[12]), .clk(and_13_out), .Q(regOut[12]), .reset(reset));  // open: Qn, preset
  D_Flip_Flop d_ff_14 (.D(regIn[13]), .clk(and_15_out), .Q(regOut[13]), .reset(reset));  // open: Qn, preset
  and and_15 (and_15_out, WE, clk);
  D_Flip_Flop d_ff_15 (.D(regIn[14]), .clk(and_14_out), .Q(regOut[14]), .reset(reset));  // open: Qn, preset
  D_Flip_Flop d_ff_16 (.D(regIn[15]), .clk(and_16_out), .Q(regOut[15]), .reset(reset));  // open: Qn, preset
  and and_16 (and_16_out, WE, clk);

  // Other names for the same wires on the sheet: in0 = regIn[0]; in1 = regIn[1]; in2 = regIn[2]; in3 = regIn[3];
  //   in4 = regIn[4]; in5 = regIn[5]; in6 = regIn[6]; in7 = regIn[7]; in8 = regIn[8]; in9 = regIn[9];
  //   in10 = regIn[10]; in11 = regIn[11]; in12 = regIn[12]; in13 = regIn[13]; in14 = regIn[14]; in15 = regIn[15];
  //   out0 = regOut[0]; out1 = regOut[1]; out2 = regOut[2]; out3 = regOut[3]; out4 = regOut[4]; out5 = regOut[5];
  //   out6 = regOut[6]; out7 = regOut[7]; out8 = regOut[8]; out9 = regOut[9]; out10 = regOut[10]; out11 = regOut[11];
  //   out12 = regOut[12]; out13 = regOut[13]; out14 = regOut[14]; out15 = regOut[15]
endmodule

module opCodeControl (
  input  [3:0] opCode,
  output addi_control,
  output alu_digit3,
  output alu_digit2,
  output alu_digit1,
  output memWriteEn,
  output regWriteEn,
  output screenEn,
  output KEYEN
);

  wire decoder_1_out0, decoder_1_out1, decoder_1_out2, decoder_1_out3, decoder_1_out4, decoder_1_out5,
       decoder_1_out6, decoder_1_out7, decoder_1_out13;

  Decoder #(.select(4)) decoder_1 (
    .out0(decoder_1_out0), .out1(decoder_1_out1), .out2(decoder_1_out2), .out3(decoder_1_out3),
    .out4(decoder_1_out4), .out5(decoder_1_out5), .out6(decoder_1_out6), .out7(decoder_1_out7),
    .out8(memWriteEn), .out13(decoder_1_out13), .out14(KEYEN), .out15(screenEn), .sel(opCode));  // open: out9, out10, out11, out12, en
  or regWrEn (regWriteEn, KEYEN, decoder_1_out13, decoder_1_out7, decoder_1_out6, decoder_1_out5, decoder_1_out4, decoder_1_out3, decoder_1_out2, decoder_1_out1, decoder_1_out0);
  or or_1 (addi_control, memWriteEn, decoder_1_out2, decoder_1_out7);
  or or_2 (alu_digit3, decoder_1_out6, decoder_1_out5);
  or or_3 (alu_digit2, decoder_1_out3, decoder_1_out4);
  or or_4 (alu_digit1, decoder_1_out1, decoder_1_out6, decoder_1_out3);
endmodule

module Format (
  input  [15:0] instruction,
  output [2:0] shamt,
  output [2:0] rd_writeReg,
  output [2:0] rt_read1,
  output [2:0] rs_read2,
  output [5:0] immediate,
  output [15:0] jAddress,
  output [3:0] opCode
);


  assign immediate = instruction[5:0];
  assign jAddress = {4'b0000, instruction[11:0]};
  assign opCode = instruction[15:12];
  assign rd_writeReg = instruction[5:3];
  assign rs_read2 = instruction[11:9];
  assign rt_read1 = instruction[8:6];
  assign shamt = instruction[2:0];
endmodule

module leftShift (
  input  [15:0] data,
  input  [2:0] shiftAmount,
  output [15:0] shifted
);

  wire multiplexer_1_out, multiplexer_2_out, multiplexer_3_out, multiplexer_4_out, multiplexer_5_out,
       multiplexer_6_out, multiplexer_7_out, multiplexer_8_out, multiplexer_9_out, multiplexer_10_out,
       multiplexer_11_out, multiplexer_12_out, multiplexer_13_out, multiplexer_14_out, multiplexer_15_out,
       multiplexer_16_out, multiplexer_17_out, multiplexer_18_out, multiplexer_19_out, multiplexer_20_out,
       multiplexer_21_out, multiplexer_22_out, multiplexer_23_out, multiplexer_24_out, multiplexer_25_out,
       multiplexer_26_out, multiplexer_27_out, multiplexer_28_out, multiplexer_29_out, multiplexer_30_out,
       multiplexer_31_out, multiplexer_32_out, not_1_out, not_2_out, not_3_out;

  Multiplexer #(.enable("false")) multiplexer_1 (.in0(1'b0), .in1(data[0]), .out(multiplexer_1_out), .sel(not_1_out));
  Multiplexer #(.enable("false")) multiplexer_2 (
    .in0(data[0]), .in1(data[1]), .out(multiplexer_2_out), .sel(not_1_out));
  Multiplexer #(.enable("false")) multiplexer_3 (
    .in0(data[1]), .in1(data[2]), .out(multiplexer_3_out), .sel(not_1_out));
  Multiplexer #(.enable("false")) multiplexer_4 (
    .in0(data[2]), .in1(data[3]), .out(multiplexer_4_out), .sel(not_1_out));
  Multiplexer #(.enable("false")) multiplexer_5 (
    .in0(data[3]), .in1(data[4]), .out(multiplexer_5_out), .sel(not_1_out));
  Multiplexer #(.enable("false")) multiplexer_6 (
    .in0(data[4]), .in1(data[5]), .out(multiplexer_6_out), .sel(not_1_out));
  Multiplexer #(.enable("false")) multiplexer_7 (
    .in0(data[5]), .in1(data[6]), .out(multiplexer_7_out), .sel(not_1_out));
  Multiplexer #(.enable("false")) multiplexer_8 (
    .in0(data[6]), .in1(data[7]), .out(multiplexer_8_out), .sel(not_1_out));
  Multiplexer #(.enable("false")) multiplexer_9 (
    .in0(data[7]), .in1(data[8]), .out(multiplexer_9_out), .sel(not_1_out));
  Multiplexer #(.enable("false")) multiplexer_10 (
    .in0(data[8]), .in1(data[9]), .out(multiplexer_10_out), .sel(not_1_out));
  Multiplexer #(.enable("false")) multiplexer_11 (
    .in0(data[9]), .in1(data[10]), .out(multiplexer_11_out), .sel(not_1_out));
  Multiplexer #(.enable("false")) multiplexer_12 (
    .in0(data[10]), .in1(data[11]), .out(multiplexer_12_out), .sel(not_1_out));
  Multiplexer #(.enable("false")) multiplexer_13 (
    .in0(data[11]), .in1(data[12]), .out(multiplexer_13_out), .sel(not_1_out));
  Multiplexer #(.enable("false")) multiplexer_14 (
    .in0(data[12]), .in1(data[13]), .out(multiplexer_14_out), .sel(not_1_out));
  Multiplexer #(.enable("false")) multiplexer_15 (
    .in0(data[13]), .in1(data[14]), .out(multiplexer_15_out), .sel(not_1_out));
  Multiplexer #(.enable("false")) multiplexer_16 (
    .in0(data[14]), .in1(data[15]), .out(multiplexer_16_out), .sel(not_1_out));
  not not_1 (not_1_out, shiftAmount[0]);
  not not_2 (not_2_out, shiftAmount[1]);
  Multiplexer #(.enable("false")) multiplexer_17 (
    .in0(1'b0), .in1(multiplexer_1_out), .out(multiplexer_17_out), .sel(not_2_out));
  Multiplexer #(.enable("false")) multiplexer_18 (
    .in0(1'b0), .in1(multiplexer_2_out), .out(multiplexer_18_out), .sel(not_2_out));
  Multiplexer #(.enable("false")) multiplexer_19 (
    .in0(multiplexer_1_out), .in1(multiplexer_3_out), .out(multiplexer_19_out), .sel(not_2_out));
  Multiplexer #(.enable("false")) multiplexer_20 (
    .in0(multiplexer_2_out), .in1(multiplexer_4_out), .out(multiplexer_20_out), .sel(not_2_out));
  Multiplexer #(.enable("false")) multiplexer_21 (
    .in0(multiplexer_3_out), .in1(multiplexer_5_out), .out(multiplexer_21_out), .sel(not_2_out));
  Multiplexer #(.enable("false")) multiplexer_22 (
    .in0(multiplexer_4_out), .in1(multiplexer_6_out), .out(multiplexer_22_out), .sel(not_2_out));
  Multiplexer #(.enable("false")) multiplexer_23 (
    .in0(multiplexer_5_out), .in1(multiplexer_7_out), .out(multiplexer_23_out), .sel(not_2_out));
  Multiplexer #(.enable("false")) multiplexer_24 (
    .in0(multiplexer_6_out), .in1(multiplexer_8_out), .out(multiplexer_24_out), .sel(not_2_out));
  Multiplexer #(.enable("false")) multiplexer_25 (
    .in0(multiplexer_7_out), .in1(multiplexer_9_out), .out(multiplexer_25_out), .sel(not_2_out));
  Multiplexer #(.enable("false")) multiplexer_26 (
    .in0(multiplexer_8_out), .in1(multiplexer_10_out), .out(multiplexer_26_out), .sel(not_2_out));
  Multiplexer #(.enable("false")) multiplexer_27 (
    .in0(multiplexer_9_out), .in1(multiplexer_11_out), .out(multiplexer_27_out), .sel(not_2_out));
  Multiplexer #(.enable("false")) multiplexer_28 (
    .in0(multiplexer_10_out), .in1(multiplexer_12_out), .out(multiplexer_28_out), .sel(not_2_out));
  Multiplexer #(.enable("false")) multiplexer_29 (
    .in0(multiplexer_11_out), .in1(multiplexer_13_out), .out(multiplexer_29_out), .sel(not_2_out));
  Multiplexer #(.enable("false")) multiplexer_30 (
    .in0(multiplexer_12_out), .in1(multiplexer_14_out), .out(multiplexer_30_out), .sel(not_2_out));
  Multiplexer #(.enable("false")) multiplexer_31 (
    .in0(multiplexer_13_out), .in1(multiplexer_15_out), .out(multiplexer_31_out), .sel(not_2_out));
  Multiplexer #(.enable("false")) multiplexer_32 (
    .in0(multiplexer_14_out), .in1(multiplexer_16_out), .out(multiplexer_32_out), .sel(not_2_out));
  Multiplexer #(.enable("false")) multiplexer_33 (
    .in0(1'b0), .in1(multiplexer_17_out), .out(shifted[0]), .sel(not_3_out));
  Multiplexer #(.enable("false")) multiplexer_34 (
    .in0(1'b0), .in1(multiplexer_18_out), .out(shifted[1]), .sel(not_3_out));
  Multiplexer #(.enable("false")) multiplexer_35 (
    .in0(1'b0), .in1(multiplexer_19_out), .out(shifted[2]), .sel(not_3_out));
  Multiplexer #(.enable("false")) multiplexer_36 (
    .in0(1'b0), .in1(multiplexer_20_out), .out(shifted[3]), .sel(not_3_out));
  Multiplexer #(.enable("false")) multiplexer_37 (
    .in0(multiplexer_17_out), .in1(multiplexer_21_out), .out(shifted[4]), .sel(not_3_out));
  Multiplexer #(.enable("false")) multiplexer_38 (
    .in0(multiplexer_18_out), .in1(multiplexer_22_out), .out(shifted[5]), .sel(not_3_out));
  Multiplexer #(.enable("false")) multiplexer_39 (
    .in0(multiplexer_19_out), .in1(multiplexer_23_out), .out(shifted[6]), .sel(not_3_out));
  Multiplexer #(.enable("false")) multiplexer_40 (
    .in0(multiplexer_20_out), .in1(multiplexer_24_out), .out(shifted[7]), .sel(not_3_out));
  Multiplexer #(.enable("false")) multiplexer_41 (
    .in0(multiplexer_21_out), .in1(multiplexer_25_out), .out(shifted[8]), .sel(not_3_out));
  Multiplexer #(.enable("false")) multiplexer_42 (
    .in0(multiplexer_22_out), .in1(multiplexer_26_out), .out(shifted[9]), .sel(not_3_out));
  Multiplexer #(.enable("false")) multiplexer_43 (
    .in0(multiplexer_23_out), .in1(multiplexer_27_out), .out(shifted[10]), .sel(not_3_out));
  Multiplexer #(.enable("false")) multiplexer_44 (
    .in0(multiplexer_24_out), .in1(multiplexer_28_out), .out(shifted[11]), .sel(not_3_out));
  Multiplexer #(.enable("false")) multiplexer_45 (
    .in0(multiplexer_25_out), .in1(multiplexer_29_out), .out(shifted[12]), .sel(not_3_out));
  Multiplexer #(.enable("false")) multiplexer_46 (
    .in0(multiplexer_26_out), .in1(multiplexer_30_out), .out(shifted[13]), .sel(not_3_out));
  Multiplexer #(.enable("false")) multiplexer_47 (
    .in0(multiplexer_27_out), .in1(multiplexer_31_out), .out(shifted[14]), .sel(not_3_out));
  Multiplexer #(.enable("false")) multiplexer_48 (
    .in0(multiplexer_28_out), .in1(multiplexer_32_out), .out(shifted[15]), .sel(not_3_out));
  not not_3 (not_3_out, shiftAmount[2]);
endmodule

module rightShift (
  input  [15:0] data,
  input  [2:0] shiftAmount,
  output [15:0] out_3
);

  leftShift leftshift_1 (
    .data({data[0], data[1], data[2], data[3], data[4], data[5], data[6], data[7], data[8], data[9], data[10], data[11], data[12], data[13], data[14], data[15]}),
    .shiftAmount(shiftAmount),
    .shifted({out_3[0], out_3[1], out_3[2], out_3[3], out_3[4], out_3[5], out_3[6], out_3[7], out_3[8], out_3[9], out_3[10], out_3[11], out_3[12], out_3[13], out_3[14], out_3[15]}));
endmodule
