// Logisim project signExtender.circ as structural Verilog: 1 circuit, main circuit signExtender
module signExtender (
  input  [5:0] \input ,
  output [15:0] \output 
);

  Multiplexer #(.width(10), .enable("false")) multiplexer_1 (
    .in0({10{1'b0}}), .in1({10{1'b1}}), .out(\output [15:6]), .sel(\input [5]));

  assign \output [5:0] = \input ;

  // Other names for the same wires on the sheet: neg = \input [5]
endmodule
